// Logisim project Logisim_simulation.circ as structural Verilog: 13 circuits, main circuit main_CPU
module main_CPU (
  input  in_1,
  input  [31:0] in_2,
  input  in_3
);

  wire ALU_SRC, and_1_out, and_2_out, and_3_out, and_4_out, and_10_out, and_13_out, and_14_out, and_15_out,
       and_16_out, and_17_out, and_18_out, and_19_out, and_20_out, and_21_out, and_22_out, and_23_out,
       and_24_out, and_25_out, and_26_out, and_27_out, and_28_out, and_29_out, and_30_out, and_31_out,
       and_32_out, and_33_out, and_34_out, and_35_out, and_36_out, AUIPC, Branch, button_2_out, CLK, CLK0,
       CLK1, comparator_1_eq, counter_3_carry, counter_5_carry, counter_7_carry, counter_8_carry,
       counter_10_carry, counter_11_carry, CPU_CLK_SRC, data_memory_1_str, EN, GCLK0, GCLK1, GPH0, GPH1,
       H_SYNC, HALT, hlt, multiplexer_4_out, multiplexer_5_out, multiplexer_6_out, multiplexer_7_out,
       multiplexer_8_out, multiplexer_10_out, nALU_TO_WB, nIMM_TO_WB, not_2_out, not_3_out, not_4_out,
       not_5_out, not_9_out, not_10_out, not_11_out, not_12_out, not_13_out, not_14_out, not_15_out,
       not_16_out, not_17_out, not_18_out, not_19_out, not_20_out, not_21_out, not_22_out, not_23_out,
       not_24_out, not_25_out, not_26_out, not_27_out, not_28_out, not_29_out, not_30_out, not_31_out,
       not_32_out, not_33_out, not_34_out, not_35_out, not_36_out, not_37_out, not_38_out, not_39_out,
       not_40_out, not_41_out, not_42_out, not_43_out, or_1_out, or_2_out, or_3_out, PC_SRC_0, PC_SRC_1, PH0,
       PH1, RAM_TO_WB, RST, s_r_ff_1_q, s_r_ff_2_q, STR_TO_RAM, STR_TO_RF, TAKE_BRANCH, undriven, V_SYNC,
       X_RST, Y_RST;
  wire [1:0] nor_1_out;
  wire [2:0] IMM_GEN_CTR_0_3, instruction_memory_1_out_7_3;
  wire [3:0] counter_7_q, counter_8_q, counter_9_q, counter_10_q, counter_11_q, counter_12_q,
       data_memory_1_str_sel, register_9_q, undriven_3;
  wire [4:0] counter_3_q, instruction_memory_1_out_7_2, instruction_memory_1_out_7_4,
       instruction_memory_1_out_7_5, register_6_q;
  wire [6:0] instruction_memory_1_out_7;
  wire [7:0] register_11_q, rom_1_p2, rom_1_p3, rom_1_p4, rom_1_p5;
  wire [7:2] rom_3_data, rom_4_data;
  wire [7:3] rom_2_data;
  wire [8:0] counter_5_q;
  wire [8:8] counter_3_q_3;
  wire [10:0] controlled_buffer_4_out, counter_3_q_2, data_memory_1_gpu_addr, GPU_ADR, multiplexer_3_out,
       register_4_q, register_7_q;
  wire [18:0] rom_1_p1;
  wire [23:0] multiplexer_9_out, rgb_video_1_p5;
  wire [31:0] cla_alu_1_output, controlled_buffer_1_out, controlled_buffer_3_out, controlled_buffer_5_out,
       counter_1_q, counter_2_q, data_memory_1_gpu_data, imm_generator_1_out, multiplexer_1_out,
       multiplexer_2_out, program_counter_2_1_out, program_counter_2_1_x, PULS, register_1_q, register_2_q,
       register_3_q, register_5_q, register_8_q, register_10_q, register_file_1_rb_0, register_file_1_rb_1,
       undriven_2;
  wire [31:25] instruction_memory_1_out_7_6;

  // NOT_Gate not_1 is placed but not wired
  Button button_1 (.out(RST));
  and and_1 (and_1_out, AUIPC, PH0);
  or or_1 (or_1_out, and_1_out, and_2_out);
  and and_2 (and_2_out, ~AUIPC, PH1);  // AND_Gate
  not not_2 (not_2_out, CLK1);
  Clock clock_1 (.out(CPU_CLK_SRC));
  Button button_2 (.out(button_2_out));
  Pull_Resistor pull_resistor_1 (.node(HALT));
  and and_3 (and_3_out, or_1_out, PC_SRC_0);
  and and_4 (and_4_out, or_1_out, PC_SRC_1);
  or or_2 (or_2_out, CPU_CLK_SRC, button_2_out);
  and and_5 (CLK, or_2_out, ~HALT);  // AND_Gate
  Program_counter_2 program_counter_2_1 (
    .X(program_counter_2_1_x), .OUT(program_counter_2_1_out), .SRC1(and_4_out), .CLK(not_2_out),
    .T_BRCH(TAKE_BRANCH), .SRC0(and_3_out), .BRCH(Branch), .RST(RST), .Y(imm_generator_1_out),
    .OUT_in(controlled_buffer_1_out));
  Register #(.width(32)) register_1 (
    .D(program_counter_2_1_out), .en(1'b1), .Q(register_1_q), .clk(CLK0));  // open: clr
  not not_3 (not_3_out, CLK);
  D_Flip_Flop d_ff_1 (.clk(not_3_out), .D(GPH0), .Q(GPH1), .Qn(GPH0));  // open: preset, reset
  not not_4 (not_4_out, CLK);
  D_Flip_Flop d_ff_2 (.clk(not_4_out), .D(PH0), .Q(PH1), .Qn(PH0));  // open: preset, reset
  // Probe on program_counter_2_1_x
  // ROM #(.addrWidth(19), .line("quad")) rom_1: pin names not known; wires that end beside it: rom_1_p1, rom_1_p2, rom_1_p3, rom_1_p4, rom_1_p5
  Instruction_memory instruction_memory_1 (
    .out_6(rom_1_p1),
    .out_7({instruction_memory_1_out_7_6, instruction_memory_1_out_7_5, instruction_memory_1_out_7_4, instruction_memory_1_out_7_3, instruction_memory_1_out_7_2, instruction_memory_1_out_7}),
    .in_2(rom_1_p2), .in_3(rom_1_p3), .in_4(rom_1_p4), .in_5(rom_1_p5), .in(program_counter_2_1_x));
  and and_6 (GCLK1, CLK, GPH1);
  and and_7 (GCLK0, CLK, GPH0);
  and and_8 (CLK1, CLK, PH1);
  and and_9 (CLK0, CLK, PH0);
  Imm_generator imm_generator_1 (
    .Out(imm_generator_1_out), .Sel(IMM_GEN_CTR_0_3),
    .Ins({instruction_memory_1_out_7_6, instruction_memory_1_out_7_5, instruction_memory_1_out_7_4, instruction_memory_1_out_7_3, instruction_memory_1_out_7_2, instruction_memory_1_out_7}));
  // Probe on imm_generator_1_out
  not not_5 (not_5_out, nIMM_TO_WB);
  assign controlled_buffer_1_out = not_5_out ? imm_generator_1_out : 32'bz;  // Controlled_Buffer controlled_buffer_1
  // Probe on {instruction_memory_1_out_7_6, instruction_memory_1_out_7_5, instruction_memory_1_out_7_4, instruction_memory_1_out_7_3, instruction_memory_1_out_7_2, instruction_memory_1_out_7}
  ROM #(.addrWidth(7)) rom_2 (
    .addr(instruction_memory_1_out_7),
    .data({rom_2_data[7], ALU_SRC, RAM_TO_WB, rom_2_data[4:3], IMM_GEN_CTR_0_3}));
  ROM #(.addrWidth(7)) rom_3 (
    .addr(instruction_memory_1_out_7),
    .data({rom_3_data[7], TAKE_BRANCH, AUIPC, PC_SRC_1, PC_SRC_0, rom_3_data[2], STR_TO_RAM, STR_TO_RF}));
  Multiplexer #(.enable("false"), .width(32)) multiplexer_1 (
    .in0(controlled_buffer_1_out), .in1(register_1_q), .out(multiplexer_1_out), .sel(or_3_out));
  or or_3 (or_3_out, PC_SRC_0, PC_SRC_1);
  Register_file register_file_1 (
    .RB_0(register_file_1_rb_0), .RB_1(register_file_1_rb_1), .Store(and_10_out), .Clock(CLK1), .Load(PH0),
    .read_register_1(instruction_memory_1_out_7_4), .read_register_2(instruction_memory_1_out_7_5),
    .write_data(multiplexer_1_out), .write_register(instruction_memory_1_out_7_2));
  and and_10 (and_10_out, PH1, STR_TO_RF);
  Register #(.width(32)) register_2 (.D(register_file_1_rb_0), .en(1'b1), .Q(register_2_q), .clk(CLK0));  // open: clr
  Register #(.width(32)) register_3 (.D(register_file_1_rb_1), .en(1'b1), .Q(register_3_q), .clk(CLK0));  // open: clr
  not not_6 (nIMM_TO_WB, rom_2_data[3]);
  not not_7 (nALU_TO_WB, rom_2_data[4]);
  Multiplexer #(.enable("false"), .width(32)) multiplexer_2 (
    .in0(register_3_q), .in1(imm_generator_1_out), .out(multiplexer_2_out), .sel(ALU_SRC));
  not not_8 (nor_1_out[1], ALU_SRC);
  Comparator #(.width(32)) comparator_1 (.a(in_2), .b(PULS), .eq(comparator_1_eq));  // open: gt, lt
  and and_11 (hlt, comparator_1_eq, in_3);
  CLA_ALU cla_alu_1 (
    .branch(Branch), .Output(cla_alu_1_output), .Y(multiplexer_2_out), .X(register_2_q),
    .i(instruction_memory_1_out_7_6[30]), .Funct3(instruction_memory_1_out_7_3), .mode(TAKE_BRANCH),
    .ALU_OP(nor_1_out));
  nor nor_1 (nor_1_out[0], STR_TO_RAM, RAM_TO_WB);
  // Probe on cla_alu_1_output
  not not_9 (not_9_out, nALU_TO_WB);
  assign controlled_buffer_1_out = not_9_out ? cla_alu_1_output : 32'bz;  // Controlled_Buffer controlled_buffer_2
  Counter #(.max('hffffffff), .width(32)) counter_1 (
    .Q(counter_1_q), .clk(CLK), .clr(RST));  // open: load, D, count, carry
  Counter #(.max('hffffffff), .trigger("falling"), .width(32)) counter_2 (
    .Q(counter_2_q), .clk(CLK), .clr(RST));  // open: load, D, count, carry
  // Probe on PULS
  Adder #(.width(32)) adder_1 (.a(counter_1_q), .b(counter_2_q), .out(PULS));  // open: cin, cout
  // Probe on controlled_buffer_1_out
  Data_memory data_memory_1 (
    .STR(data_memory_1_str), .STR_SEL(data_memory_1_str_sel), .GPU_ADDR(data_memory_1_gpu_addr),
    .GPU_DATA(data_memory_1_gpu_data), .out_7(controlled_buffer_1_out), .Load(RAM_TO_WB), .Store(STR_TO_RAM),
    .Clock(CLK1), .Funct3(instruction_memory_1_out_7_3), .Data(register_3_q), .Adress(cla_alu_1_output));  // open: out_9, Exception
  and and_12 (HALT, in_1, undriven);
  and and_13 (and_13_out, undriven, CLK1);
  Register #(.width(11)) register_4 (.Q(register_4_q), .clk(and_13_out));  // open: D, en, clr
  Register #(.width(32)) register_5 (.D(undriven_2), .Q(register_5_q), .clk(and_13_out));  // open: en, clr
  S_R_Flip_Flop s_r_ff_1 (
    .S(undriven), .clk(and_13_out), .R(1'b0), .Q(s_r_ff_1_q), .reset(and_14_out));  // open: Qn, preset
  Register #(.width(5)) register_6 (.D({undriven_3, STR_TO_RAM}), .Q(register_6_q), .clk(and_13_out));  // open: en, clr
  not not_10 (not_10_out, PH0);
  and and_14 (and_14_out, ~CLK0, s_r_ff_2_q);  // AND_Gate
  S_R_Flip_Flop s_r_ff_2 (
    .S(s_r_ff_1_q), .clk(CLK0), .R(1'b0), .Q(s_r_ff_2_q), .reset(and_14_out));  // open: Qn, preset
  Multiplexer #(.enable("false"), .width(11)) multiplexer_3 (
    .in0(register_4_q), .in1(GPU_ADR), .out(multiplexer_3_out), .sel(not_10_out));
  and and_15 (and_15_out, ~not_10_out, s_r_ff_1_q);  // AND_Gate
  assign controlled_buffer_3_out = and_15_out ? register_5_q : 32'bz;  // Controlled_Buffer controlled_buffer_3
  LED led_1 (.in(and_16_out));
  and and_16 (and_16_out, s_r_ff_2_q, s_r_ff_1_q);
  and and_17 (and_17_out, and_16_out, register_6_q[1]);
  and and_18 (and_18_out, and_16_out, register_6_q[2]);
  and and_19 (and_19_out, and_16_out, register_6_q[3]);
  and and_20 (and_20_out, and_16_out, register_6_q[4]);
  and and_21 (and_21_out, data_memory_1_str, CLK1);
  not not_11 (not_11_out, and_17_out);
  not not_12 (not_12_out, not_11_out);
  not not_13 (not_13_out, and_18_out);
  not not_14 (not_14_out, not_13_out);
  not not_15 (not_15_out, and_19_out);
  not not_16 (not_16_out, not_15_out);
  not not_17 (not_17_out, and_20_out);
  not not_18 (not_18_out, not_17_out);
  Counter #(.max('h108), .width(9)) counter_3 (
    .Q({counter_3_q_3[8], counter_3_q_2[2:0], counter_3_q}), .carry(counter_3_carry), .clk(GCLK0));  // open: load, D, count, clr
  Counter #(.max('h96)) counter_4 (.Q(counter_3_q_2[10:3]), .clk(counter_3_carry));  // open: load, D, count, carry, clr
  assign controlled_buffer_4_out = GPH0 ? register_7_q : 11'bz;  // Controlled_Buffer controlled_buffer_4
  Register #(.width(11)) register_7 (.D(data_memory_1_gpu_addr), .Q(register_7_q), .clk(and_21_out));  // open: en, clr
  assign controlled_buffer_5_out = GPH0 ? register_8_q : 32'bz;  // Controlled_Buffer controlled_buffer_5
  Register #(.width(32)) register_8 (.D(data_memory_1_gpu_data), .Q(register_8_q), .clk(and_21_out));  // open: en, clr
  Register #(.width(4)) register_9 (.D(data_memory_1_str_sel), .Q(register_9_q), .clk(and_21_out));  // open: en, clr
  and and_22 (and_22_out, PH1, not_19_out);
  not not_19 (not_19_out, s_r_ff_1_q);
  and and_23 (and_23_out, not_12_out, and_17_out);
  and and_24 (and_24_out, not_14_out, and_18_out);
  and and_25 (and_25_out, not_16_out, and_19_out);
  and and_26 (and_26_out, not_18_out, and_20_out);
  assign controlled_buffer_4_out = GPH1 ? counter_3_q_2 : 11'bz;  // Controlled_Buffer controlled_buffer_6
  and and_27 (and_27_out, GCLK0, register_9_q[0]);
  and and_28 (and_28_out, GCLK0, register_9_q[1]);
  and and_29 (and_29_out, GCLK0, register_9_q[2]);
  and and_30 (and_30_out, GCLK0, register_9_q[3]);
  RAM #(.addrWidth(11), .databus("bidir")) ram_1 (
    .addr(multiplexer_3_out), .data(controlled_buffer_3_out[7:0]));  // open: we, oe, clk
  RAM #(.addrWidth(11), .databus("bidir")) ram_2 (
    .addr(multiplexer_3_out), .data(controlled_buffer_3_out[15:8]));  // open: we, oe, clk
  RAM #(.addrWidth(11), .databus("bidir")) ram_3 (
    .addr(multiplexer_3_out), .data(controlled_buffer_3_out[23:16]));  // open: we, oe, clk
  RAM #(.addrWidth(11), .databus("bidir")) ram_4 (
    .addr(multiplexer_3_out), .data(controlled_buffer_3_out[31:24]));  // open: we, oe, clk
  not not_20 (not_20_out, and_27_out);
  not not_21 (not_21_out, not_20_out);
  not not_22 (not_22_out, and_28_out);
  not not_23 (not_23_out, not_22_out);
  not not_24 (not_24_out, and_29_out);
  not not_25 (not_25_out, not_24_out);
  not not_26 (not_26_out, and_30_out);
  not not_27 (not_27_out, not_26_out);
  and and_31 (and_31_out, not_21_out, and_27_out);
  and and_32 (and_32_out, not_23_out, and_28_out);
  and and_33 (and_33_out, not_25_out, and_29_out);
  and and_34 (and_34_out, not_27_out, and_30_out);
  RAM #(.addrWidth(11), .databus("bidir")) ram_5 (
    .addr(controlled_buffer_4_out), .data(controlled_buffer_5_out[7:0]));  // open: we, oe, clk
  RAM #(.addrWidth(11), .databus("bidir")) ram_6 (
    .addr(controlled_buffer_4_out), .data(controlled_buffer_5_out[15:8]));  // open: we, oe, clk
  RAM #(.addrWidth(11), .databus("bidir")) ram_7 (
    .addr(controlled_buffer_4_out), .data(controlled_buffer_5_out[23:16]));  // open: we, oe, clk
  RAM #(.addrWidth(11), .databus("bidir")) ram_8 (
    .addr(controlled_buffer_4_out), .data(controlled_buffer_5_out[31:24]));  // open: we, oe, clk
  Pull_Resistor pull_resistor_2 (.node(controlled_buffer_3_out));
  Counter #(.max('h108), .width(9)) counter_5 (
    .Q({counter_5_q[8], GPU_ADR[2:0], counter_5_q[4:0]}), .carry(counter_5_carry), .clk(CLK0));  // open: load, D, count, clr
  not not_28 (not_28_out, GCLK1);
  Counter #(.max('h96)) counter_6 (.Q(GPU_ADR[10:3]), .clk(counter_5_carry));  // open: load, D, count, carry, clr
  Multiplexer #(.enable("false"), .select(4)) multiplexer_4 (
    .in0(controlled_buffer_3_out[0]), .in1(controlled_buffer_3_out[1]), .in2(controlled_buffer_3_out[2]),
    .in3(controlled_buffer_3_out[3]), .in4(controlled_buffer_3_out[4]), .in5(controlled_buffer_3_out[5]),
    .in6(controlled_buffer_3_out[6]), .in7(controlled_buffer_3_out[7]), .in8(controlled_buffer_3_out[8]),
    .in9(controlled_buffer_3_out[9]), .in10(controlled_buffer_3_out[10]), .in11(controlled_buffer_3_out[11]),
    .in12(controlled_buffer_3_out[12]), .in13(controlled_buffer_3_out[13]),
    .in14(controlled_buffer_3_out[14]), .in15(controlled_buffer_3_out[15]), .out(multiplexer_4_out),
    .sel(counter_5_q[3:0]));
  Multiplexer #(.enable("false"), .select(4)) multiplexer_5 (
    .in0(controlled_buffer_3_out[16]), .in1(controlled_buffer_3_out[17]), .in2(controlled_buffer_3_out[18]),
    .in3(controlled_buffer_3_out[19]), .in4(controlled_buffer_3_out[20]), .in5(controlled_buffer_3_out[21]),
    .in6(controlled_buffer_3_out[22]), .in7(controlled_buffer_3_out[23]), .in8(controlled_buffer_3_out[24]),
    .in9(controlled_buffer_3_out[25]), .in10(controlled_buffer_3_out[26]),
    .in11(controlled_buffer_3_out[27]), .in12(controlled_buffer_3_out[28]),
    .in13(controlled_buffer_3_out[29]), .in14(controlled_buffer_3_out[30]),
    .in15(controlled_buffer_3_out[31]), .out(multiplexer_5_out), .sel(counter_5_q[3:0]));
  not not_29 (not_29_out, not_28_out);
  not not_30 (not_30_out, not_29_out);
  not not_31 (not_31_out, not_30_out);
  not not_32 (not_32_out, not_31_out);
  Multiplexer multiplexer_6 (
    .in0(multiplexer_4_out), .in1(multiplexer_5_out), .out(multiplexer_6_out), .sel(counter_5_q[4]), .en(1'b1));
  not not_33 (not_33_out, not_32_out);
  not not_34 (not_34_out, not_33_out);
  not not_35 (not_35_out, not_34_out);
  not not_36 (not_36_out, not_35_out);
  Register #(.width(32)) register_10 (.D(controlled_buffer_5_out), .Q(register_10_q), .clk(GCLK1));  // open: en, clr
  not not_37 (not_37_out, not_36_out);
  not not_38 (not_38_out, not_37_out);
  not not_39 (not_39_out, not_38_out);
  not not_40 (not_40_out, not_39_out);
  not not_41 (not_41_out, not_40_out);
  not not_42 (not_42_out, not_41_out);
  not not_43 (not_43_out, not_42_out);
  Multiplexer #(.enable("false"), .select(4)) multiplexer_7 (
    .in0(register_10_q[0]), .in1(register_10_q[1]), .in2(register_10_q[2]), .in3(register_10_q[3]),
    .in4(register_10_q[4]), .in5(register_10_q[5]), .in6(register_10_q[6]), .in7(register_10_q[7]),
    .in8(register_10_q[8]), .in9(register_10_q[9]), .in10(register_10_q[10]), .in11(register_10_q[11]),
    .in12(register_10_q[12]), .in13(register_10_q[13]), .in14(register_10_q[14]), .in15(register_10_q[15]),
    .out(multiplexer_7_out), .sel(counter_3_q[3:0]));
  Multiplexer #(.enable("false"), .select(4)) multiplexer_8 (
    .in0(register_10_q[16]), .in1(register_10_q[17]), .in2(register_10_q[18]), .in3(register_10_q[19]),
    .in4(register_10_q[20]), .in5(register_10_q[21]), .in6(register_10_q[22]), .in7(register_10_q[23]),
    .in8(register_10_q[24]), .in9(register_10_q[25]), .in10(register_10_q[26]), .in11(register_10_q[27]),
    .in12(register_10_q[28]), .in13(register_10_q[29]), .in14(register_10_q[30]), .in15(register_10_q[31]),
    .out(multiplexer_8_out), .sel(counter_3_q[3:0]));
  Multiplexer #(.enable("false"), .width(24)) multiplexer_9 (
    .in0({24{1'b0}}), .in1({24{1'b1}}), .out(multiplexer_9_out), .sel(multiplexer_6_out));
  // RGB_Video #(.height(256), .width(256)) rgb_video_1: pin names not known; wires that end beside it: not_43_out, 1'b1, {counter_3_q_2[2:0], counter_3_q}, counter_3_q_2[10:3], rgb_video_1_p5
  Multiplexer #(.enable("false")) multiplexer_10 (
    .in0(multiplexer_7_out), .in1(multiplexer_8_out), .out(multiplexer_10_out), .sel(counter_3_q[4]));
  // RGB_Video #(.cursor("No Cursor"), .height(256), .width(256)) rgb_video_2: pin names not known; wires that end beside it: CLK1, 1'b1, {GPU_ADR[2:0], counter_5_q[4:0]}, GPU_ADR[10:3], multiplexer_9_out
  Multiplexer #(.enable("false"), .width(24)) multiplexer_11 (
    .in0({24{1'b0}}), .in1({24{1'b1}}), .out(rgb_video_1_p5), .sel(multiplexer_10_out));
  and and_35 (and_35_out, GCLK0, X_RST);
  and and_36 (and_36_out, GCLK0, Y_RST);
  Counter #(.max('h0), .ongoal("continue"), .width(4)) counter_7 (
    .Q(counter_7_q), .carry(counter_7_carry), .clk(GCLK0), .clr(and_35_out));  // open: load, D, count
  Counter #(.max('h0), .ongoal("continue"), .width(4)) counter_8 (
    .Q(counter_8_q), .carry(counter_8_carry), .clk(counter_7_carry), .clr(and_35_out));  // open: load, D, count
  Counter #(.max('hf), .width(4)) counter_9 (
    .Q(counter_9_q), .clk(counter_8_carry), .clr(and_35_out));  // open: load, D, count, carry
  Counter #(.max('hf), .width(4)) counter_10 (
    .Q(counter_10_q), .carry(counter_10_carry), .clk(and_35_out), .clr(and_36_out));  // open: load, D, count
  Counter #(.max('hf), .width(4)) counter_11 (
    .Q(counter_11_q), .carry(counter_11_carry), .clk(counter_10_carry), .clr(and_36_out));  // open: load, D, count
  Counter #(.max('hf), .width(4)) counter_12 (
    .Q(counter_12_q), .clk(counter_11_carry), .clr(and_36_out));  // open: load, D, count, carry
  // Probe on {counter_3_q_3[8], counter_3_q_2[2:0], counter_3_q}
  ROM #(.addrWidth(17)) rom_4 (
    .addr({2'b00, counter_3_q_2[10:3], counter_3_q_3[8], counter_3_q_2[2:0], counter_3_q[4:3], counter_3_q[0]}),
    .data({rom_4_data, Y_RST, X_RST}));
  // Probe on 7'b1010000
  Register register_11 (
    .D({rom_4_data, 2'b00}), .Q({register_11_q[7:5], EN, V_SYNC, H_SYNC, register_11_q[1:0]}), .clk(GCLK0));  // open: en, clr
  // NOT_Gate not_44 is placed but not wired

  // Notes on the sheet:
  //   CLOCK
  //   TR* = Temporary register
  //   TR2
  //   STORED PROGRAM
  //   contents of rom_2 (hex, n*v repeats v):
  //   0 0 0 60 15*0 50 0 0 0 3 11*0 41 15*0 10 0 0 0 b 43*0 2 0 0 0 10 7*0 4
  //   contents of rom_3 (hex, n*v repeats v):
  //   0 0 0 1 15*0 1 0 0 0 29 11*0 2 15*0 1 0 0 0 1 43*0 48 0 0 0 11 7*0 9
  //   TR0
  //   TR1
  //   Halt at pulse
  //   Utilities
  //   to_fix: unsigned loads (byte/half) need 0 all the way
  //   Pulse Count
  //   Work in progress
  //   store
  //   Address
  //   Data
  //   Horizontal
  //   Vertical
  //   contents of rom_4 (hex, n*v repeats v):
  //   compressed eJztzTEKgDAMhtG9p8icqZUivf/JVArilMX1QYbAx89bPXuMfUeOGWfe73z+WLu1or27VrTPrhWN
  //   x+PxeDwej8fj8Xg8Ho/H4/F4PB6Px+P99C4HEdi9
endmodule

module Register_file (
  input  Store,
  input  Clock,
  input  Load,
  input  [4:0] read_register_1,
  input  [4:0] read_register_2,
  input  [31:0] write_data,
  input  [4:0] write_register,
  output [31:0] RB_0,
  output [31:0] RB_1
);

  wire and_1_out, and_2_out, and_3_out, and_4_out, and_5_out, and_6_out, buffer_1_out, buffer_2_out, is_zero,
       is_zero_r1, is_zero_r2, not_1_out, not_2_out, not_3_out, not_4_out, not_5_out, not_6_out, not_7_out,
       not_8_out, not_9_out, not_10_out, not_11_out, not_12_out, not_13_out, not_14_out, not_15_out,
       not_16_out, not_17_out, not_18_out;
  wire [4:0] controlled_buffer_1_out, controlled_buffer_3_out;

  and and_1 (and_1_out, Store, is_zero);
  and and_2 (and_2_out, Load, is_zero_r1);
  and and_3 (and_3_out, Store, is_zero);
  and and_4 (and_4_out, Load, is_zero_r2);
  assign controlled_buffer_1_out = not_1_out ? read_register_1 : 5'bz;  // Controlled_Buffer controlled_buffer_1
  not not_1 (not_1_out, and_1_out);
  assign controlled_buffer_1_out = buffer_1_out ? write_register : 5'bz;  // Controlled_Buffer controlled_buffer_2
  buf buffer_1 (buffer_1_out, and_1_out);
  and and_5 (and_5_out, and_1_out, Clock);
  not not_2 (not_2_out, and_5_out);
  not not_3 (not_3_out, not_2_out);
  not not_4 (not_4_out, not_3_out);
  not not_5 (not_5_out, not_4_out);
  assign controlled_buffer_3_out = not_6_out ? read_register_2 : 5'bz;  // Controlled_Buffer controlled_buffer_3
  not not_6 (not_6_out, and_3_out);
  assign controlled_buffer_3_out = buffer_2_out ? write_register : 5'bz;  // Controlled_Buffer controlled_buffer_4
  buf buffer_2 (buffer_2_out, and_3_out);
  and and_6 (and_6_out, and_3_out, Clock);
  not not_7 (not_7_out, and_6_out);
  not not_8 (not_8_out, not_7_out);
  not not_9 (not_9_out, not_8_out);
  not not_10 (not_10_out, not_9_out);
  RAM #(.addrWidth(5), .dataWidth(16), .databus("bidir")) ram_1 (
    .addr(controlled_buffer_1_out), .data(RB_0[15:0]));  // open: we, oe, clk
  RAM #(.addrWidth(5), .dataWidth(16), .databus("bidir")) ram_2 (
    .addr(controlled_buffer_1_out), .data(RB_0[31:16]));  // open: we, oe, clk
  RAM #(.addrWidth(5), .dataWidth(16), .databus("bidir")) ram_3 (
    .addr(controlled_buffer_3_out), .data(RB_1[15:0]));  // open: we, oe, clk
  RAM #(.addrWidth(5), .dataWidth(16), .databus("bidir")) ram_4 (
    .addr(controlled_buffer_3_out), .data(RB_1[31:16]));  // open: we, oe, clk
  not not_11 (not_11_out, and_1_out);
  not not_12 (not_12_out, not_11_out);
  not not_13 (not_13_out, and_3_out);
  not not_14 (not_14_out, not_13_out);
  assign RB_0 = not_16_out ? write_data : 32'bz;  // Controlled_Buffer controlled_buffer_5
  Pull_Resistor pull_resistor_1 (.node(RB_0));
  not not_15 (not_15_out, not_12_out);
  not not_16 (not_16_out, not_15_out);
  Pull_Resistor pull_resistor_2 (.node(RB_1));
  assign RB_1 = not_18_out ? write_data : 32'bz;  // Controlled_Buffer controlled_buffer_6
  not not_17 (not_17_out, not_14_out);
  not not_18 (not_18_out, not_17_out);
  or or_1 (is_zero_r1, read_register_1[0], read_register_1[1], read_register_1[2], read_register_1[3], read_register_1[4]);
  or or_2 (is_zero_r2, read_register_2[0], read_register_2[1], read_register_2[2], read_register_2[3], read_register_2[4]);
  or or_3 (is_zero, write_register[0], write_register[1], write_register[2], write_register[3], write_register[4]);

  // Other names for the same wires on the sheet: clk = Clock; Read_reg1[4:0] = read_register_1;
  //   Read_reg2[4:0] = read_register_2; Register_bank_0[31:0] = RB_0; Register_bank_1[31:0] = RB_1; str = Store;
  //   Write_reg[4:0] = write_register

  // Notes on the sheet:
  //   Inputs
  //   Register Bank 0
  //   Register Bank 1
  //   REGISTER FILE
  //   Outputs
  //   Logic
endmodule

module CLA_ALU (
  input  [2:0] Funct3,
  input  [1:0] ALU_OP,
  input  i,
  input  [31:0] Y,
  input  [31:0] X,
  input  mode,
  output [31:0] Output,
  output branch
);

  wire and_5_out, and_6_out, and_7_out, and_8_out, and_9_out, and_10_out, and_11_out, and_12_out, and_13_out,
       and_14_out, and_15_out, and_16_out, and_17_out, and_18_out, C1, C2, C3, C4, C5, G1, G2, G3, G4, i_t,
       not_1_out, or_2_out, or_3_out, or_4_out, or_9_out, P0, P1, P2, P3, P4, shifter_1_sh_out;
  wire [0:0] or_1_out, rom_1_data;
  wire [2:0] f3;
  wire [6:2] rom_6_data;
  wire [30:0] rom_1_data_2;
  wire [31:0] alu_reference_1_1_out_6;

  and and_1 (f3[2], Funct3[2], ALU_OP[0]);
  and and_2 (i_t, i, ALU_OP[1]);
  and and_3 (f3[1], Funct3[1], ALU_OP[0]);
  and and_4 (f3[0], Funct3[0], ALU_OP[0]);
  ROM #(.addrWidth(18)) rom_1 (
    .addr({Y[5:0], X[5:0], i_t, f3, 1'b0, mode}), .data({C1, P0, rom_1_data_2[4:0], rom_1_data[0]}));
  ROM #(.addrWidth(18)) rom_2 (.addr({Y[11:6], X[11:6], i_t, f3, C1, mode}), .data({G1, P1, rom_1_data_2[10:5]}));
  ROM #(.addrWidth(18)) rom_3 (.addr({Y[17:12], X[17:12], i_t, f3, C2, mode}), .data({G2, P2, rom_1_data_2[16:11]}));
  ROM #(.addrWidth(18)) rom_4 (.addr({Y[23:18], X[23:18], i_t, f3, C3, mode}), .data({G3, P3, rom_1_data_2[22:17]}));
  ROM #(.addrWidth(18)) rom_5 (.addr({Y[29:24], X[29:24], i_t, f3, C4, mode}), .data({G4, P4, rom_1_data_2[28:23]}));
  ROM #(.addrWidth(18)) rom_6 (
    .addr({4'b0000, Y[31:30], 4'b0000, X[31:30], i_t, f3, C5, mode}),
    .data({branch, rom_6_data, rom_1_data_2[30:29]}));
  LED P (.in(P0));
  LED G (.in(C1));
  LED P_2 (.in(P1));
  LED G_2 (.in(G1));
  LED P_3 (.in(P2));
  LED G_3 (.in(G2));
  LED P_4 (.in(P3));
  LED G_4 (.in(G3));
  LED P_5 (.in(P4));
  LED G_5 (.in(G4));
  LED Set_bit (.in(rom_6_data[6]));
  LED u_branch (.in(branch));
  ALU_reference_1 alu_reference_1_1 (
    .I(i_t), .SRC_1(X), .SRC_2(Y), .Funct3(f3), .out_6(alu_reference_1_1_out_6));  // open: Zero, Branch
  shifter shifter_1 (.out_5(Output), .SH_out(shifter_1_sh_out), .in_1(i_t), .in_2(Funct3), .in_3(X), .in_4(Y[4:0]));
  or or_1 (or_1_out[0], rom_6_data[6], rom_1_data[0]);
  // Probe on alu_reference_1_1_out_6
  not not_1 (not_1_out, shifter_1_sh_out);
  assign Output = not_1_out ? {rom_1_data_2, or_1_out[0]} : 32'bz;  // Controlled_Buffer controlled_buffer_1
  and and_5 (and_5_out, C1, P1);
  or or_2 (or_2_out, and_5_out, G1);
  and and_6 (and_6_out, or_2_out, P2);
  or or_3 (or_3_out, and_6_out, G2);
  and and_7 (and_7_out, C1, P1);
  and and_8 (and_8_out, G1, P2);
  and and_9 (and_9_out, C1, P1, P2);
  and and_10 (and_10_out, G2, P3);
  and and_11 (and_11_out, P3, P2, G1);
  and and_12 (and_12_out, C1, P1, P2, P3);
  and and_13 (and_13_out, G3, P4);
  and and_14 (and_14_out, G2, P3, P4);
  and and_15 (and_15_out, G1, P2, P3, P4);
  and and_16 (and_16_out, C1, P1, P2, P3, P4);
  and and_17 (and_17_out, or_3_out, P3);
  or or_4 (or_4_out, and_17_out, G3);
  or or_5 (C2, and_7_out, G1);
  or or_6 (C3, and_8_out, and_9_out, G2);
  or or_7 (C4, and_10_out, and_11_out, and_12_out, G3);
  or or_8 (C5, and_13_out, and_14_out, and_15_out, and_16_out, G4);
  and and_18 (and_18_out, or_4_out, P4);
  or or_9 (or_9_out, and_18_out, G4);

  // Other names for the same wires on the sheet: M = mode; G0 = C1; _f3[2:0] = Funct3

  // Notes on the sheet:
  //   contents of rom_1 (hex, n*v repeats v):
  //   compressed eJy8XU1i2zoP3PMUWnflOGmbHqdN4/sf4XsESWAGGFlK3C+L5xezAkVzwB8Jw8Fle71sT/3jsr2M
  //   j/YCX+ZHw4LX8SHLXuzP2+3f1fj03/+uG5a8futNHv+N0vaqS16+udVmVg2vsZ9eSq7/lTxTyX+W
  //   7VpaoUueSkv5ut6uWtLv90Il3bKXrpY0+yddcqUSsmzrN9SSfr/vVNItX0ZLWvx6XfJMJW7ZsN9q
  //   Sb/fj5b6tpe271u6TpS8bMWyzd8Q15WSfr+fBc8fvSWElS6hugxPvq53Xi3p93stePbS1ZLRebrk
  //   B5WQpWNVS/r9fhU8X0dLECtZ8rPgadcxVqWk3+93wfO/0vZrS9eJktetWLb5G+K6UtLv96fg+bu3
  //   hLDSJVSX4cnX9c6rJf1+bwXPXrpaMjpPl/ymErJ0rGpJv9/fgufbaAlgpUv+FDztOsKqlvT7vRc8
  //   /yttf7d0nSh524plm78hrisl/X63gud7bwlhpUuoLsOTr+udV0v6/Z4uBdBevJoyek+XvFMJWTpY
  //   tcRu+PRUIB3lFwJst+xWcJ2XEmqyzBbIa0G3l7entCrull22at/Wz4JrRVm/9VNdWZ9s2eSVdL+s
  //   rq/5Wlv5VVm/9VNdZUc5r6r7ZXWthWsDalXWb/1UV9xRzivsflldd+e1jLUq67d+qqtvL29PvGbu
  //   l9U1+KkvueVaUdZv/VRX4qcf1i7Geresrsf5WsNalfVbP9VVeZTzKrxfVtdmuDawVmX91k91hR7l
  //   vCLvl9V1el7LWKuyfuunulr38vbEa+x+WV2zn/oSXa4VZf3WT3Xlfvpt7WKsd8vq+p2vNaxVWb/1
  //   U13FRzmv2vtldS2HawNrVdZv/VRX9FHOK/h+WV3X57WMtSrrt36qq3svb0+8Ju+X1TX+qS/p5VpR
  //   1m/9VFf6p3drF2O9W1bX+3ytYa3K+q2vl4q/bQZ4kd8vq0s/XBtYizK79bUu/6P8Qrjulj3V9X9e
  //   S7jKMnuQrut/L2/X9Ay8W3bZqn1bvwuuFWX91lfxZG2Pw+lJerdMPF+na+0JW5XZo3Jd/0c5r/X7
  //   ZXX9h2sDa1XWb32t6/8o57V+v6yu//NaxlqV9Vtf6/rfy9uV1+r9srr+X/taX64VZf3W17r+X39Y
  //   uxjr3bK6/udrDWtV1m99rev/KOe1fr+srv9wbWCtyvqtr3X9H+W81u+X1fV/XstYq7J+62td/3t5
  //   u/JavV9W1/9rX+vLtaKs3/pa1//rb2sXY71bVtf/fK1hrcr6ra91/R/lvNbvl9X1H64NrFVZv/W1
  //   rv+jnNf6/bK6/s9rGWtV1m99ret/L29XXqv3y+r6f+1rfblWlPVbX+v6f323djHWu2V1/c/XGtaq
  //   rN/6+VLxt30Br/X7ZXX9h2sDa1Fmt36u6/8ovxCuu2XXuv7PawlXWdZv/VzX/17ennmt3i+7bNW+
  //   rd8F14oye7Fe1//nq7WLcN0vq+t/vtbep6syewUu3rJbeXqrvlsm3rXHtYG1KrPX5nX9H+W81u+X
  //   1fV/XstYq7J+6+e6/vfy9sxr9X5ZXf+f+1pfrhVl/dbPdf1//mHtYqx3y+r6n681rFVZv/VzXf9H
  //   Oa/1+2V1/YdrA2tV1m/9XNf/Uc5r/X5ZXf/ntYy1Kuu3fq7rfy9vz7xW75fV9f+5r/XlWlHWb/1c
  //   1//n39Yuxnq3rK7/+VrDWpX1Wz/X9X+U81q/X1bXf7g2sFZl/dbPdf0f5bzW75fV9X9ey1irsn7r
  //   57r+9/L2zGv1flld/5/7Wl+uFWX91s91/X9+t3Yx1rtldf3P1xrWouxnv7VFlhP+ti/gtX6/rK7/
  //   cG1gLco8jh3o40+Zfz2NS//7eOnvRvBbj6r/95EQZHOoo00rruM6ws123Yq1v3DgffRRK5H4/6p8
  //   6TW9UJ0jnnL7dzU+N4yFu5f0DmV/KCU13t9XS95x1JK+yn7P9zMWwJUt27hftNQCGqWllRewWuqW
  //   dj9e3fo9e2m0pPdrLXmm2pcP43XDFWpJvx+vaN1yRvfBK5flU3OMV08fMAWmJXjtjIOnGcti1+TF
  //   taTXxfuXadl4B1FL+v145emWffPxgy3buG+0tl9TPEHwAlbsPfC0OHjBs5dGS3rn1ZKfW+YOZMvR
  //   ebWk349XqG45o/uA1bIMPF+3wh0IS8BqWgKeMw6e8LTYNWFVS3pdrwXPvprxjqCW9PvxStIt+2bi
  //   N1u2cd9obb+meILgBazYe+BpcfCCZy+NlvTOqyV/tswdyJaj82pJvx+vON1yRvcBq2UZeL5tmTsA
  //   loDVtAQ8Vxw8AWrrDIFVS3plbwXQ/njKS3wtsRs+lYnTiADvbNtmE73B/ZriDIIasKLvAekMfxdQ
  //   R3kijomy25ZJBNV6dKMss4A0P1Ca/WUigBsFtw+IV+w/YSxpAssccPbYdwJ6xqkJRllmdV4K3BaO
  //   TjF9WdZv/VRX2cEJuCb7thoR7bfr6loreQIeewfwR+y7gm/lvMLKsme+j8NP106oVZnFo+vq63F+
  //   hN/tAf4V+8/4K57Askf8V+w74z/i1Iy1KrM663ps4egU05dl/dZPdVUenIAfyb6tRkT77bq6Nkue
  //   gMfeAf8R+674WzmvyLLsJ9/H8adrJ9aqzOLRdbX2OD/i7/aA/4r9Z/wVT2DZI/4r9p3xH3FqxlqV
  //   WZ11/bZwdIrpy7J+66e6ig9OwO9k31Yjov12XV3LJU/AY++A/4h9V/ytnFdwWfaH7+P407UTa1Vm
  //   8ei6unucH/F3e8B/xf4z/oonsOwR/xX7zviPODVjrcqszrrcWzg6xfRVmd36Wpf8wQl4T/ZtNSLa
  //   b9fVhV/yBDz2HvjP2HfBf5TzQq/KOPYf+PO1o3NlmT0U1uXf4/yAa9gH/h77T/hLnsCyB/w99p3w
  //   n3FqwlWWWZ11/bdwdIrpy7J+66t4yrbH7Guyb7MR0H67TjxrK56Ax94B/xH7rvhbOa/1suyZ7+P4
  //   07UTa1Vm8ei6/nucH/F3e8B/xf4z/oonsOwR/xX7zviPODVjrcqszrr+Wzg6xfRlWb/1ta7/gxPw
  //   I9m32Qhov11X13/JE/DYO+A/Yt8VfyvntV6W/eT7OP507cRalVk8uq7/HudH/N0e8F+x/4y/4gks
  //   e8R/xb4z/iNOzVirMquzrv8Wjk4xfVnWb32t6//gBPxO9m02Atpv19X1X/IEPPYO+I/Yd8Xfynmt
  //   l2V/+D6OP107sVZlFo+u67/H+RF/twf8V+w/4694Asse8V+x74z/iFMz1qrM6qzrv4WjU0xfldmt
  //   n+v6PzgB78m+zUZA++26uv5LnoDH3gP/Gfsu+I9yXutVGcf+A3++dnSuLLN4dF3/Pc4PuIZ94O+x
  //   /4S/5Akse8DfY98J/xmnJlxlmdVZ138LR6eYvizrt36u6//gBKT37Paindf/cV1d/yVPwGPvgP+I
  //   fVf8rTy9YVdlz3wfx5+unVirMotH1/Xf4/yIv9sD/iv2n/FXPIFlj/iv2HfGf8SpGWtVZnXW9d/C
  //   0SmmL8v6rZ/r+j84AT+SfZuNgPbbdXX9lzwBj70D/iP2XfG3cl7rZdlPvo/jT9dOrFWZxaPr+u9x
  //   fsTf7QH/FfvP+CuewLJH/FfsO+M/4tSMtSqzOuv6b+HoFNOXZf3Wz3X9H5yA38m+zUZA++26uv5L
  //   noDH3gH/Efuu+Fs5r/Wy7A/fx/GnayfWqszi0XX99zg/4u/2gP+K/Wf8FU9g2WMcbsW+M/4jTs1Y
  //   qzKrs67//dqWYvqq7K3f+q2u/4MT8J7s22wE4G/X1fVf8gQ89g77v17E6GNVE9Rr/599WKTcvq0o
  //   +s3CM4xqMre/Uh0Nv81T3ogBG9uHBef7Rxs285szANqN+yuZex3tOe4LdbSX/sf3cd1Hz+df+9f5
  //   MX/Zgyf+VY06Ol7P96+4eiB15sT/iuMHUp8/Ia5P/P9/T4jrE/+fPyFe4/iztT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
  //   contents of rom_2 (hex, n*v repeats v):
  //   compressed eJy8XUtiHLcO3PMUvc5qJDm2chxHlu5/hBd+AFQBxemWxs+LjDVMg81hgZ9uFAu349vteOofN/to
  //   +GV9tFzQr1Nl38afHx+/r8an//55PvqX1/nRXv/qTZ7/zdL2qku+/eVWx7BqeE3/qCXP/5W8UMl/
  //   lu25tEKXPJWW8nW9XbWk3+8blXTLXmotaeN/6ZJnKiHLZr+hlvT7/U0l3fLbbEmLX69LXqjELRv2
  //   Wy3p9/veUt/20vb3ka4TJd+OYtnWb4jrSkm/34+C5/feEsJKl1BdA0++rndeLen3ey149lJryew8
  //   XfKdSsjSsaol/X7/FDxfZ0sQK1nyo+A5rmOsSkm/38+C53+l7Z8jXSdKXo9i2dZviOtKSb/fvwXP
  //   n70lhJUuoboGnnxd77xa0u/3VvDspdaS2Xm65CeVkKVjVUv6/X4VPN9mSwArXfJvwXNcR1jVkn6/
  //   94Lnf6Xt15GuEyVvR7Fs6zfEdaWk3++j4PneW0JY6RKqa+DJ1/XOqyX9fk+3AmgvtqbM3tMl71RC
  //   lg5WLRk3fHoqkM7yGwG2LfsouK5LCTVZNhbI54JuL29PaVXclt2Oat/sZ8G1oqzf+qmurE9j2eSV
  //   dF9W19d87Vj5VVm/9VNdZWc5r6r7srrWwrUBtSrrt36qK+4s5xV2X1bX3XUtY63K+q2f6urby9sT
  //   r5n7sroGP/Ult1wryvqtn+pK/PR9tIux3pbV9ThfO7BWZf3WT3VVnuW8Cu/L6toM1wbWqqzf+qmu
  //   0LOcV+R9WV2n17WMtSrrt36qq3Uvb0+8xu7L6pr91Jfocq0o67d+qiv308/RLsZ6W1bX73ztwFqV
  //   9Vs/1VV8lvOqvS+razlcG1irsn7rp7qiz3JewfdldV1f1zLWqqzf+qmu7r28PfGavC+ra/xTX9LL
  //   taKs3/qprvRP76NdjPW2rK73+dqBtSrrt36+VfzHZoAX+X1ZXfrh2sBalI1bP9flf5bfCNdt2VNd
  //   /9e1hKssGw/Sdf3v5e05PQNvy25HtW/2u+BaUdZv/SyerMfjcHqS3paJ5+t07XjCVmXjUbmu/7Oc
  //   1/p9WV3/4drAWpX1Wz/X9X+W81q/L6vr/7qWsVZl/dbPdf3v5e2Z1+p9WV3/n/taX64VZf3Wz3X9
  //   f/4+2sVYb8vq+p+vHVirsn7r57r+z3Je6/dldf2HawNrVdZv/VzX/1nOa/2+rK7/61rGWpX1Wz/X
  //   9b+Xt2deq/dldf1/7mt9uVaU9Vs/1/X/+edoF2O9Lavrf752YK3K+q2f6/o/y3mt35fV9R+uDaxV
  //   Wb/1c13/Zzmv9fuyuv6vaxlrVdZv/VzX/17ennmt3pfV9f+5r/XlWlHWb/1c1//n99EuxnpbVtf/
  //   fO3AWpX1W7/cKv5jX8Br/b6srv9wbWAtysatX+r6P8tvhOu27Lmu/+tawlWW9Vu/1PW/l7cXXqv3
  //   Zbej2jf7XXCtKBsv1uv6//I82kW47svq+p+vHe/TVdl4BS7eso/y9FZ9Wybetce1gbUqG6/N6/o/
  //   y3mt35fV9X9dy1irsn7rl7r+9/L2wmv1vqyu/y99rS/XirJ+65e6/r98H+1irLdldf3P1w6sVVm/
  //   9Utd/2c5r/X7srr+w7WBtSrrt36p6/8s57V+X1bX/3UtY63K+q1f6vrfy9sLr9X7srr+v/S1vlwr
  //   yvqtX+r6//JztIux3pbV9T9fO7BWZf3WL3X9n+W81u/L6voP1wbWqqzf+qWu/7Oc1/p9WV3/17WM
  //   tSrrt36p638vby+8Vu/L6vr/0tf6cq0o67d+qev/y/toF2O9Lavrf752YC3KfvRbj6Bywn/sC3it
  //   35fV9R+uDaxFmcexA338Keuvp3npfx/f+rsR/Naj6v99JATZHOpoy4rreO6x+BcOs6vAu4rZPzXj
  //   CsTHDO6neP9DNb40jIW7l/QOZX8oJTXe31dL3nHUkr7K/p3vN1gAz2zZ5v2iP0dAo7S08gKspW45
  //   7serW79nL42WdPxqyQvVbj6M101XqCX9fryidcsV3QevNMun5n5jPX3CFFiW4LUrDp5mrBG7Ji+u
  //   Jb0u3r8sy8Y7iFrS78crT7fsm4/vbNnmfaO1/ZriCYIXYLH3wHPEwQuevTRa0juvlvw4MncgW87O
  //   qyX9frxCdcsV3QeszDLwfD0KdyAsAatlCXiuOHjCc8SuCata0ut6LXj21Yx3BLWk349Xkm7ZNxM/
  //   2bLN+0Zr+zXFEwQvwGLvgeeIgxc8e2m0pHdeLfn3yNyBbDk7r5b0+/GK0y1XdB+wMsvA8+3I3AGw
  //   BKyWJeBpcfAE6FhnCKxa0it7K4D2x1Ne4mvJuOFTmTgHEeCdbdtqoje4X1OcQVADLPoekK7wdwF1
  //   lifimCj7ODKJoFrPbpRlIyDND5TD/rYQwI2C2wfEFvtPGEuagJkDzh77TkCvODXBKMtGnbcC9whH
  //   p5i+LOu3fqqr7OQEPCf7Zo2I9o/r6loreQIeewfwZ+y7gj/KeYWVZS98H4efrl1Qq7IRj66rr8f5
  //   EX63B/gt9p/xVzwBs0f8Lfad8Z9xasZalY0663o8wtEppi/L+q2f6qo8OQHfk32zRkT7x3V1bZY8
  //   AY+9A/4z9l3xH+W8IsuyH3wfx5+uXVirshGPrqu1x/kRf7cH/C32n/FXPAGzR/wt9p3xn3FqxlqV
  //   jTrr+j3C0SmmL8v6rZ/qKj45AT+TfbNGRPvHdXUtlzwBj70D/jP2XfEf5byCy7J/+T6OP127sFZl
  //   Ix5dV3eP8yP+bg/4W+w/4694AmaP+FvsO+M/49SMtSobddblfoSjU0xflY1bP9clf3IC3pN9s0ZE
  //   +8d1deGXPAGPvQf+K/Zd8J/lvNCrMo79B/587excWTYeCuvy73F+wDXsA3+P/Sf8JU/A7AF/j30n
  //   /FecmnCVZaPOuv6PcHSK6cuyfutn8ZQ9HrOfk31bjYD2j+vEs7biCXjsHfCfse+K/yjntV6WvfB9
  //   HH+6dmGtykY8uq7/HudH/N0e8LfYf8Zf8QTMHvG32HfGf8apGWtVNuqs6/8IR6eYvizrt36u6//k
  //   BHxP9m01Ato/rqvrv+QJeOwd8J+x74r/KOe1Xpb94Ps4/nTtwlqVjXh0Xf89zo/4uz3gb7H/jL/i
  //   CZg94m+x74z/jFMz1qps1FnX/xGOTjF9WdZv/VzX/8kJ+Jns22oEtH9cV9d/yRPw2DvgP2PfFf9R
  //   zmu9LPuX7+P407ULa1U24tF1/fc4P+Lv9oC/xf4z/oonYPaIv8W+M/4zTs1Yq7JRZ13/Rzg6xfRV
  //   2bj1S13/JyfgPdm31Qho/7iurv+SJ+Cx98B/xb4L/rOc13pVxrH/wJ+vnZ0ry0Y8uq7/HucHXMM+
  //   8PfYf8Jf8gTMHvD32HfCf8WpCVdZNuqs6/8IR6eYvizrt36p6//kBKT37ONFO6//87q6/kuegMfe
  //   Af8Z+674j/L0hl2VvfB9HH+6dmGtykY8uq7/HudH/N0e8LfYf8Zf8QTMHvG32HfGf8apGWtVNuqs
  //   6/8IR6eYvizrt36p6//kBHxP9m01Ato/rqvrv+QJeOwd8J+x74r/KOe1Xpb94Ps4/nTtwlqVjXh0
  //   Xf89zo/4uz3gb7H/jL/iCZg94m+x74z/jFMz1qps1FnX/xGOTjF9WdZv/VLX/8kJ+Jns22oEtH9c
  //   V9d/yRPw2DvgP2PfFf9Rzmu9LPuX7+P407ULa1U24tF1/fc4P+Lv9oC/xf4z/oonYPYYh7PYd8Z/
  //   xqkZa1U26qzrf7+2pZi+Knvrt36r6//kBLwn+7YaAfiP6+r6L3kCHnuH/V8vYvSxqgXqc/9nfIxI
  //   +fhmUfSPEZ5hVJP5+CvV0fDbOuWNGLDx+HgZP7jfZNqsb84AaB/cX8nc62gvcV+oo33rjvD3187n
  //   P/e/+OPBE/+qRh0dr+f7La4eSF058W9x/EDq6yfE9Yn//+8JcX3i/+snxGscf7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
  //   contents of rom_3 (hex, n*v repeats v):
  //   compressed eJy8XUtiHLcO3PMUvc5qJDm2chxHlu5/hBd+AFQBxemWxs+LjDVMg81hgZ9uFAu349vteOofN/to
  //   +GV9tFzQr1Nl38afHx+/r8an//55PvqX1/nRXv/qTZ7/zdL2qku+/eVWx7BqeE3/qCXP/5W8UMl/
  //   lu25tEKXPJWW8nW9XbWk3+8blXTLXmotaeN/6ZJnKiHLZr+hlvT7/U0l3fLbbEmLX69LXqjELRv2
  //   Wy3p9/veUt/20vb3ka4TJd+OYtnWb4jrSkm/34+C5/feEsJKl1BdA0++rndeLen3ey149lJryew8
  //   XfKdSsjSsaol/X7/FDxfZ0sQK1nyo+A5rmOsSkm/38+C53+l7Z8jXSdKXo9i2dZviOtKSb/fvwXP
  //   n70lhJUuoboGnnxd77xa0u/3VvDspdaS2Xm65CeVkKVjVUv6/X4VPN9mSwArXfJvwXNcR1jVkn6/
  //   94Lnf6Xt15GuEyVvR7Fs6zfEdaWk3++j4PneW0JY6RKqa+DJ1/XOqyX9fk+3AmgvtqbM3tMl71RC
  //   lg5WLRk3fHoqkM7yGwG2LfsouK5LCTVZNhbI54JuL29PaVXclt2Oat/sZ8G1oqzf+qmurE9j2eSV
  //   dF9W19d87Vj5VVm/9VNdZWc5r6r7srrWwrUBtSrrt36qK+4s5xV2X1bX3XUtY63K+q2f6urby9sT
  //   r5n7sroGP/Ult1wryvqtn+pK/PR9tIux3pbV9ThfO7BWZf3WT3VVnuW8Cu/L6toM1wbWqqzf+qmu
  //   0LOcV+R9WV2n17WMtSrrt36qq3Uvb0+8xu7L6pr91Jfocq0o67d+qiv308/RLsZ6W1bX73ztwFqV
  //   9Vs/1VV8lvOqvS+razlcG1irsn7rp7qiz3JewfdldV1f1zLWqqzf+qmu7r28PfGavC+ra/xTX9LL
  //   taKs3/qprvRP76NdjPW2rK73+dqBtSrrt36+VfzHZoAX+X1ZXfrh2sBalI1bP9flf5bfCNdt2VNd
  //   /9e1hKssGw/Sdf3v5e05PQNvy25HtW/2u+BaUdZv/SyerMfjcHqS3paJ5+t07XjCVmXjUbmu/7Oc
  //   1/p9WV3/4drAWpX1Wz/X9X+W81q/L6vr/7qWsVZl/dbPdf3v5e2Z1+p9WV3/n/taX64VZf3Wz3X9
  //   f/4+2sVYb8vq+p+vHVirsn7r57r+z3Je6/dldf2HawNrVdZv/VzX/1nOa/2+rK7/61rGWpX1Wz/X
  //   9b+Xt2deq/dldf1/7mt9uVaU9Vs/1/X/+edoF2O9Lavrf752YK3K+q2f6/o/y3mt35fV9R+uDaxV
  //   Wb/1c13/Zzmv9fuyuv6vaxlrVdZv/VzX/17ennmt3pfV9f+5r/XlWlHWb/1c1//n99EuxnpbVtf/
  //   fO3AWpX1W7/cKv5jX8Br/b6srv9wbWAtysatX+r6P8tvhOu27Lmu/+tawlWW9Vu/1PW/l7cXXqv3
  //   Zbej2jf7XXCtKBsv1uv6//I82kW47svq+p+vHe/TVdl4BS7eso/y9FZ9Wybetce1gbUqG6/N6/o/
  //   y3mt35fV9X9dy1irsn7rl7r+9/L2wmv1vqyu/y99rS/XirJ+65e6/r98H+1irLdldf3P1w6sVVm/
  //   9Utd/2c5r/X7srr+w7WBtSrrt36p6/8s57V+X1bX/3UtY63K+q1f6vrfy9sLr9X7srr+v/S1vlwr
  //   yvqtX+r6//JztIux3pbV9T9fO7BWZf3WL3X9n+W81u/L6voP1wbWqqzf+qWu/7Oc1/p9WV3/17WM
  //   tSrrt36p638vby+8Vu/L6vr/0tf6cq0o67d+qev/y/toF2O9Lavrf752YC3KfvRbj6Bywn/sC3it
  //   35fV9R+uDaxFmcexA338Keuvp3npfx/f+rsR/Naj6v99JATZHOpoy4rreO6x+BcOs6vAu4rZPzXj
  //   CsTHDO6neP9DNb40jIW7l/QOZX8oJTXe31dL3nHUkr7K/p3vN1gAz2zZ5v2iP0dAo7S08gKspW45
  //   7serW79nL42WdPxqyQvVbj6M101XqCX9fryidcsV3QevNMun5n5jPX3CFFiW4LUrDp5mrBG7Ji+u
  //   Jb0u3r8sy8Y7iFrS78crT7fsm4/vbNnmfaO1/ZriCYIXYLH3wHPEwQuevTRa0juvlvw4MncgW87O
  //   qyX9frxCdcsV3QeszDLwfD0KdyAsAatlCXiuOHjCc8SuCata0ut6LXj21Yx3BLWk349Xkm7ZNxM/
  //   2bLN+0Zr+zXFEwQvwGLvgeeIgxc8e2m0pHdeLfn3yNyBbDk7r5b0+/GK0y1XdB+wMsvA8+3I3AGw
  //   BKyWJeBpcfAE6FhnCKxa0it7K4D2x1Ne4mvJuOFTmTgHEeCdbdtqoje4X1OcQVADLPoekK7wdwF1
  //   lifimCj7ODKJoFrPbpRlIyDND5TD/rYQwI2C2wfEFvtPGEuagJkDzh77TkCvODXBKMtGnbcC9whH
  //   p5i+LOu3fqqr7OQEPCf7Zo2I9o/r6loreQIeewfwZ+y7gj/KeYWVZS98H4efrl1Qq7IRj66rr8f5
  //   EX63B/gt9p/xVzwBs0f8Lfad8Z9xasZalY0663o8wtEppi/L+q2f6qo8OQHfk32zRkT7x3V1bZY8
  //   AY+9A/4z9l3xH+W8IsuyH3wfx5+uXVirshGPrqu1x/kRf7cH/C32n/FXPAGzR/wt9p3xn3FqxlqV
  //   jTrr+j3C0SmmL8v6rZ/qKj45AT+TfbNGRPvHdXUtlzwBj70D/jP2XfEf5byCy7J/+T6OP127sFZl
  //   Ix5dV3eP8yP+bg/4W+w/4694AmaP+FvsO+M/49SMtSobddblfoSjU0xflY1bP9clf3IC3pN9s0ZE
  //   +8d1deGXPAGPvQf+K/Zd8J/lvNCrMo79B/587excWTYeCuvy73F+wDXsA3+P/Sf8JU/A7AF/j30n
  //   /FecmnCVZaPOuv6PcHSK6cuyfutn8ZQ9HrOfk31bjYD2j+vEs7biCXjsHfCfse+K/yjntV6WvfB9
  //   HH+6dmGtykY8uq7/HudH/N0e8LfYf8Zf8QTMHvG32HfGf8apGWtVNuqs6/8IR6eYvizrt36u6//k
  //   BHxP9m01Ato/rqvrv+QJeOwd8J+x74r/KOe1Xpb94Ps4/nTtwlqVjXh0Xf89zo/4uz3gb7H/jL/i
  //   CZg94m+x74z/jFMz1qps1FnX/xGOTjF9WdZv/VzX/8kJ+Jns22oEtH9cV9d/yRPw2DvgP2PfFf9R
  //   zmu9LPuX7+P407ULa1U24tF1/fc4P+Lv9oC/xf4z/oonYPaIv8W+M/4zTs1Yq7JRZ13/Rzg6xfRV
  //   2bj1S13/JyfgPdm31Qho/7iurv+SJ+Cx98B/xb4L/rOc13pVxrH/wJ+vnZ0ry0Y8uq7/HucHXMM+
  //   8PfYf8Jf8gTMHvD32HfCf8WpCVdZNuqs6/8IR6eYvizrt36p6//kBKT37ONFO6//87q6/kuegMfe
  //   Af8Z+674j/L0hl2VvfB9HH+6dmGtykY8uq7/HudH/N0e8LfYf8Zf8QTMHvG32HfGf8apGWtVNuqs
  //   6/8IR6eYvizrt36p6//kBHxP9m01Ato/rqvrv+QJeOwd8J+x74r/KOe1Xpb94Ps4/nTtwlqVjXh0
  //   Xf89zo/4uz3gb7H/jL/iCZg94m+x74z/jFMz1qps1FnX/xGOTjF9WdZv/VLX/8kJ+Jns22oEtH9c
  //   V9d/yRPw2DvgP2PfFf9Rzmu9LPuX7+P407ULa1U24tF1/fc4P+Lv9oC/xf4z/oonYPYYh7PYd8Z/
  //   xqkZa1U26qzrf7+2pZi+Knvrt36r6//kBLwn+7YaAfiP6+r6L3kCHnuH/V8vYvSxqgXqc/9nfIxI
  //   +fhmUfSPEZ5hVJP5+CvV0fDbOuWNGLDx+HgZP7jfZNqsb84AaB/cX8nc62gvcV+oo33rjvD3187n
  //   P/e/+OPBE/+qRh0dr+f7La4eSF058W9x/EDq6yfE9Yn//+8JcX3i/+snxGscf7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
  //   contents of rom_4 (hex, n*v repeats v):
  //   compressed eJy8XUtiHLcO3PMUvc5qJDm2chxHlu5/hBd+AFQBxemWxs+LjDVMg81hgZ9uFAu349vteOofN/to
  //   +GV9tFzQr1Nl38afHx+/r8an//55PvqX1/nRXv/qTZ7/zdL2qku+/eVWx7BqeE3/qCXP/5W8UMl/
  //   lu25tEKXPJWW8nW9XbWk3+8blXTLXmotaeN/6ZJnKiHLZr+hlvT7/U0l3fLbbEmLX69LXqjELRv2
  //   Wy3p9/veUt/20vb3ka4TJd+OYtnWb4jrSkm/34+C5/feEsJKl1BdA0++rndeLen3ey149lJryew8
  //   XfKdSsjSsaol/X7/FDxfZ0sQK1nyo+A5rmOsSkm/38+C53+l7Z8jXSdKXo9i2dZviOtKSb/fvwXP
  //   n70lhJUuoboGnnxd77xa0u/3VvDspdaS2Xm65CeVkKVjVUv6/X4VPN9mSwArXfJvwXNcR1jVkn6/
  //   94Lnf6Xt15GuEyVvR7Fs6zfEdaWk3++j4PneW0JY6RKqa+DJ1/XOqyX9fk+3AmgvtqbM3tMl71RC
  //   lg5WLRk3fHoqkM7yGwG2LfsouK5LCTVZNhbI54JuL29PaVXclt2Oat/sZ8G1oqzf+qmurE9j2eSV
  //   dF9W19d87Vj5VVm/9VNdZWc5r6r7srrWwrUBtSrrt36qK+4s5xV2X1bX3XUtY63K+q2f6urby9sT
  //   r5n7sroGP/Ult1wryvqtn+pK/PR9tIux3pbV9ThfO7BWZf3WT3VVnuW8Cu/L6toM1wbWqqzf+qmu
  //   0LOcV+R9WV2n17WMtSrrt36qq3Uvb0+8xu7L6pr91Jfocq0o67d+qiv308/RLsZ6W1bX73ztwFqV
  //   9Vs/1VV8lvOqvS+razlcG1irsn7rp7qiz3JewfdldV1f1zLWqqzf+qmu7r28PfGavC+ra/xTX9LL
  //   taKs3/qprvRP76NdjPW2rK73+dqBtSrrt36+VfzHZoAX+X1ZXfrh2sBalI1bP9flf5bfCNdt2VNd
  //   /9e1hKssGw/Sdf3v5e05PQNvy25HtW/2u+BaUdZv/SyerMfjcHqS3paJ5+t07XjCVmXjUbmu/7Oc
  //   1/p9WV3/4drAWpX1Wz/X9X+W81q/L6vr/7qWsVZl/dbPdf3v5e2Z1+p9WV3/n/taX64VZf3Wz3X9
  //   f/4+2sVYb8vq+p+vHVirsn7r57r+z3Je6/dldf2HawNrVdZv/VzX/1nOa/2+rK7/61rGWpX1Wz/X
  //   9b+Xt2deq/dldf1/7mt9uVaU9Vs/1/X/+edoF2O9Lavrf752YK3K+q2f6/o/y3mt35fV9R+uDaxV
  //   Wb/1c13/Zzmv9fuyuv6vaxlrVdZv/VzX/17ennmt3pfV9f+5r/XlWlHWb/1c1//n99EuxnpbVtf/
  //   fO3AWpX1W7/cKv5jX8Br/b6srv9wbWAtysatX+r6P8tvhOu27Lmu/+tawlWW9Vu/1PW/l7cXXqv3
  //   Zbej2jf7XXCtKBsv1uv6//I82kW47svq+p+vHe/TVdl4BS7eso/y9FZ9Wybetce1gbUqG6/N6/o/
  //   y3mt35fV9X9dy1irsn7rl7r+9/L2wmv1vqyu/y99rS/XirJ+65e6/r98H+1irLdldf3P1w6sVVm/
  //   9Utd/2c5r/X7srr+w7WBtSrrt36p6/8s57V+X1bX/3UtY63K+q1f6vrfy9sLr9X7srr+v/S1vlwr
  //   yvqtX+r6//JztIux3pbV9T9fO7BWZf3WL3X9n+W81u/L6voP1wbWqqzf+qWu/7Oc1/p9WV3/17WM
  //   tSrrt36p638vby+8Vu/L6vr/0tf6cq0o67d+qev/y/toF2O9Lavrf752YC3KfvRbj6Bywn/sC3it
  //   35fV9R+uDaxFmcexA338Keuvp3npfx/f+rsR/Naj6v99JATZHOpoy4rreO6x+BcOs6vAu4rZPzXj
  //   CsTHDO6neP9DNb40jIW7l/QOZX8oJTXe31dL3nHUkr7K/p3vN1gAz2zZ5v2iP0dAo7S08gKspW45
  //   7serW79nL42WdPxqyQvVbj6M101XqCX9fryidcsV3QevNMun5n5jPX3CFFiW4LUrDp5mrBG7Ji+u
  //   Jb0u3r8sy8Y7iFrS78crT7fsm4/vbNnmfaO1/ZriCYIXYLH3wHPEwQuevTRa0juvlvw4MncgW87O
  //   qyX9frxCdcsV3QeszDLwfD0KdyAsAatlCXiuOHjCc8SuCata0ut6LXj21Yx3BLWk349Xkm7ZNxM/
  //   2bLN+0Zr+zXFEwQvwGLvgeeIgxc8e2m0pHdeLfn3yNyBbDk7r5b0+/GK0y1XdB+wMsvA8+3I3AGw
  //   BKyWJeBpcfAE6FhnCKxa0it7K4D2x1Ne4mvJuOFTmTgHEeCdbdtqoje4X1OcQVADLPoekK7wdwF1
  //   lifimCj7ODKJoFrPbpRlIyDND5TD/rYQwI2C2wfEFvtPGEuagJkDzh77TkCvODXBKMtGnbcC9whH
  //   p5i+LOu3fqqr7OQEPCf7Zo2I9o/r6loreQIeewfwZ+y7gj/KeYWVZS98H4efrl1Qq7IRj66rr8f5
  //   EX63B/gt9p/xVzwBs0f8Lfad8Z9xasZalY0663o8wtEppi/L+q2f6qo8OQHfk32zRkT7x3V1bZY8
  //   AY+9A/4z9l3xH+W8IsuyH3wfx5+uXVirshGPrqu1x/kRf7cH/C32n/FXPAGzR/wt9p3xn3FqxlqV
  //   jTrr+j3C0SmmL8v6rZ/qKj45AT+TfbNGRPvHdXUtlzwBj70D/jP2XfEf5byCy7J/+T6OP127sFZl
  //   Ix5dV3eP8yP+bg/4W+w/4694AmaP+FvsO+M/49SMtSobddblfoSjU0xflY1bP9clf3IC3pN9s0ZE
  //   +8d1deGXPAGPvQf+K/Zd8J/lvNCrMo79B/587excWTYeCuvy73F+wDXsA3+P/Sf8JU/A7AF/j30n
  //   /FecmnCVZaPOuv6PcHSK6cuyfutn8ZQ9HrOfk31bjYD2j+vEs7biCXjsHfCfse+K/yjntV6WvfB9
  //   HH+6dmGtykY8uq7/HudH/N0e8LfYf8Zf8QTMHvG32HfGf8apGWtVNuqs6/8IR6eYvizrt36u6//k
  //   BHxP9m01Ato/rqvrv+QJeOwd8J+x74r/KOe1Xpb94Ps4/nTtwlqVjXh0Xf89zo/4uz3gb7H/jL/i
  //   CZg94m+x74z/jFMz1qps1FnX/xGOTjF9WdZv/VzX/8kJ+Jns22oEtH9cV9d/yRPw2DvgP2PfFf9R
  //   zmu9LPuX7+P407ULa1U24tF1/fc4P+Lv9oC/xf4z/oonYPaIv8W+M/4zTs1Yq7JRZ13/Rzg6xfRV
  //   2bj1S13/JyfgPdm31Qho/7iurv+SJ+Cx98B/xb4L/rOc13pVxrH/wJ+vnZ0ry0Y8uq7/HucHXMM+
  //   8PfYf8Jf8gTMHvD32HfCf8WpCVdZNuqs6/8IR6eYvizrt36p6//kBKT37ONFO6//87q6/kuegMfe
  //   Af8Z+674j/L0hl2VvfB9HH+6dmGtykY8uq7/HudH/N0e8LfYf8Zf8QTMHvG32HfGf8apGWtVNuqs
  //   6/8IR6eYvizrt36p6//kBHxP9m01Ato/rqvrv+QJeOwd8J+x74r/KOe1Xpb94Ps4/nTtwlqVjXh0
  //   Xf89zo/4uz3gb7H/jL/iCZg94m+x74z/jFMz1qps1FnX/xGOTjF9WdZv/VLX/8kJ+Jns22oEtH9c
  //   V9d/yRPw2DvgP2PfFf9Rzmu9LPu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
  //   contents of rom_5 (hex, n*v repeats v):
  //   compressed eJy8XUtiHLcO3PMUvc5qJDm2chxHlu5/hBd+AFQBxemWxs+LjDVMg81hgZ9uFAu349vteOofN/to
  //   +GV9tFzQr1Nl38afHx+/r8an//55PvqX1/nRXv/qTZ7/zdL2qku+/eVWx7BqeE3/qCXP/5W8UMl/
  //   lu25tEKXPJWW8nW9XbWk3+8blXTLXmotaeN/6ZJnKiHLZr+hlvT7/U0l3fLbbEmLX69LXqjELRv2
  //   Wy3p9/veUt/20vb3ka4TJd+OYtnWb4jrSkm/34+C5/feEsJKl1BdA0++rn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
  //   contents of rom_6 (hex, n*v repeats v):
  //   compressed eJztndGS40jKhe/1FLr2le2q+UPv/2T/VlkkHCBtybOz0931xUZ4a7ITGSdwDspE4rpe19u6XdfH
  //   /7br8vV/n/bf//nj83Jdwr8//igjH2Xk83Epu8Y+vFzXNPExcvvPn3dX4T8j2+UxevPv2/qRcfX/
  //   iIrU9+iydSNf3/UhI5+7rn9dvv71a8r36OUxV3W7h+s9RrL08n0JkR4af4jGUfLj8c9fo5eHfqrj
  //   R9Ckav2QNq2jtK/6rYx8PpZ6e5ji+4+/XL3vQVfCRoKQXTAK7dZcfGTYZY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
  //   ** mode is an input from control unit - it will turn on when computing branches
  //   Lazy approach
  //   Cool approach (migh be as slow as the first one, depending on what ICs we will use)
  //   CLU
endmodule

module ALU_reference_1 (
  input  I,
  input  [31:0] SRC_1,
  input  [31:0] SRC_2,
  input  [2:0] Funct3,
  output Zero,
  output [31:0] out_6,
  output Branch
);

  wire comparator_1_lt, comparator_2_lt, comparator_3_eq, comparator_3_gt, comparator_3_lt, comparator_4_eq,
       comparator_4_gt, comparator_4_lt, not_1_out, or_2_out, or_3_out;
  wire [31:0] adder_1_out, and_1_out, bit_extender_1_out, bit_extender_2_out, multiplexer_1_out, or_1_out,
       subtractor_1_out, xor_1_out;

  Adder #(.width(32)) adder_1 (.a(SRC_1), .b(SRC_2), .out(adder_1_out));  // open: cin, cout
  Subtractor #(.width(32)) subtractor_1 (.a(SRC_1), .b(SRC_2), .out(subtractor_1_out));  // open: bin, bout
  Comparator #(.width(32)) comparator_1 (.a(SRC_1), .b(SRC_2), .lt(comparator_1_lt));  // open: gt, eq
  Comparator #(.mode("unsigned"), .width(32)) comparator_2 (
    .a(SRC_1), .b(SRC_2), .lt(comparator_2_lt));  // open: gt, eq
  assign xor_1_out = SRC_1 ^ SRC_2;  // XOR_Gate xor_1, 32 bits wide
  assign or_1_out = SRC_1 | SRC_2;  // OR_Gate or_1, 32 bits wide
  assign and_1_out = SRC_1 & SRC_2;  // AND_Gate and_1, 32 bits wide
  Comparator #(.width(32)) comparator_3 (
    .a(SRC_1), .b(SRC_2), .gt(comparator_3_gt), .eq(comparator_3_eq), .lt(comparator_3_lt));
  Comparator #(.mode("unsigned"), .width(32)) comparator_4 (
    .a(SRC_1), .b(SRC_2), .gt(comparator_4_gt), .eq(comparator_4_eq), .lt(comparator_4_lt));
  Multiplexer #(.enable("false"), .width(32)) multiplexer_1 (
    .in0(adder_1_out), .in1(subtractor_1_out), .out(multiplexer_1_out), .sel(I));
  assign bit_extender_1_out = {{31{1'b0}}, comparator_1_lt};  // Bit_Extender bit_extender_1
  assign bit_extender_2_out = {{31{1'b0}}, comparator_2_lt};  // Bit_Extender bit_extender_2
  or or_2 (or_2_out, comparator_4_gt, comparator_4_eq);
  not not_1 (not_1_out, comparator_3_eq);
  or or_3 (or_3_out, comparator_3_eq, comparator_3_gt);
  // Probe on multiplexer_1_out
  Multiplexer #(.enable("false"), .select(3)) multiplexer_2 (
    .in0(comparator_3_eq), .in1(not_1_out), .in2(1'b0), .in3(1'b0), .in4(comparator_3_lt), .in5(or_3_out),
    .in6(comparator_4_lt), .in7(or_2_out), .out(Branch), .sel(Funct3));
  Multiplexer #(.enable("false"), .select(3), .width(32)) multiplexer_3 (
    .in0(multiplexer_1_out), .in1({32{1'b0}}), .in2(bit_extender_1_out), .in3(bit_extender_2_out),
    .in4(xor_1_out), .in5({32{1'b0}}), .in6(or_1_out), .in7(and_1_out), .out(out_6), .sel(Funct3));
  Comparator #(.width(32)) comparator_5 (.a({32{1'b0}}), .b(out_6), .eq(Zero));  // open: gt, lt

  // Notes on the sheet:
  //   add
  //   sub
  //   SLL
  //   SLT
  //   SLTU
  //   XOR
  //   SRL
  //   SRA
  //   OR
  //   AND
endmodule

module ALU_reference_2 (
  input  I,
  input  [31:0] SRC_1,
  input  [31:0] SRC_2,
  input  [2:0] Funct3,
  output Zero,
  output [31:0] out_6,
  output Branch
);

  wire comparator_1_lt, comparator_2_lt, comparator_3_eq, comparator_3_gt, comparator_3_lt, comparator_4_eq,
       comparator_4_gt, comparator_4_lt, not_1_out, or_2_out, or_3_out;
  wire [31:0] adder_1_out, and_1_out, bit_extender_1_out, bit_extender_2_out, multiplexer_1_out,
       multiplexer_2_out, or_1_out, shifter_1_out, shifter_2_out, shifter_3_out, subtractor_1_out, xor_1_out;

  Adder #(.width(32)) adder_1 (.a(SRC_1), .b(SRC_2), .out(adder_1_out));  // open: cin, cout
  Subtractor #(.width(32)) subtractor_1 (.a(SRC_1), .b(SRC_2), .out(subtractor_1_out));  // open: bin, bout
  Comparator #(.width(32)) comparator_1 (.a(SRC_1), .b(SRC_2), .lt(comparator_1_lt));  // open: gt, eq
  Comparator #(.mode("unsigned"), .width(32)) comparator_2 (
    .a(SRC_1), .b(SRC_2), .lt(comparator_2_lt));  // open: gt, eq
  assign xor_1_out = SRC_1 ^ SRC_2;  // XOR_Gate xor_1, 32 bits wide
  assign or_1_out = SRC_1 | SRC_2;  // OR_Gate or_1, 32 bits wide
  assign and_1_out = SRC_1 & SRC_2;  // AND_Gate and_1, 32 bits wide
  Comparator #(.width(32)) comparator_3 (
    .a(SRC_1), .b(SRC_2), .gt(comparator_3_gt), .eq(comparator_3_eq), .lt(comparator_3_lt));
  Comparator #(.mode("unsigned"), .width(32)) comparator_4 (
    .a(SRC_1), .b(SRC_2), .gt(comparator_4_gt), .eq(comparator_4_eq), .lt(comparator_4_lt));
  Multiplexer #(.enable("false"), .width(32)) multiplexer_1 (
    .in0(adder_1_out), .in1(subtractor_1_out), .out(multiplexer_1_out), .sel(I));
  Shifter #(.width(32)) shifter_1 (.in(SRC_1), .\dist (SRC_2[4:0]), .out(shifter_1_out));
  assign bit_extender_1_out = {{31{1'b0}}, comparator_1_lt};  // Bit_Extender bit_extender_1
  assign bit_extender_2_out = {{31{1'b0}}, comparator_2_lt};  // Bit_Extender bit_extender_2
  Shifter #(.shift("lr"), .width(32)) shifter_2 (.in(SRC_1), .\dist (SRC_2[4:0]), .out(shifter_2_out));
  Shifter #(.shift("ar"), .width(32)) shifter_3 (.in(SRC_1), .\dist (SRC_2[4:0]), .out(shifter_3_out));
  or or_2 (or_2_out, comparator_4_gt, comparator_4_eq);
  Multiplexer #(.enable("false"), .width(32)) multiplexer_2 (
    .in0(shifter_2_out), .in1(shifter_3_out), .out(multiplexer_2_out), .sel(I));
  not not_1 (not_1_out, comparator_3_eq);
  or or_3 (or_3_out, comparator_3_eq, comparator_3_gt);
  // Probe on multiplexer_1_out
  Multiplexer #(.enable("false"), .select(3)) multiplexer_3 (
    .in0(comparator_3_eq), .in1(not_1_out), .in2(1'b0), .in3(1'b0), .in4(comparator_3_lt), .in5(or_3_out),
    .in6(comparator_4_lt), .in7(or_2_out), .out(Branch), .sel(Funct3));
  Multiplexer #(.enable("false"), .select(3), .width(32)) multiplexer_4 (
    .in0(multiplexer_1_out), .in1(shifter_1_out), .in2(bit_extender_1_out), .in3(bit_extender_2_out),
    .in4(xor_1_out), .in5(multiplexer_2_out), .in6(or_1_out), .in7(and_1_out), .out(out_6), .sel(Funct3));
  Comparator #(.width(32)) comparator_5 (.a({32{1'b0}}), .b(out_6), .eq(Zero));  // open: gt, lt

  // Notes on the sheet:
  //   add
  //   sub
  //   SLL
  //   SLT
  //   SLTU
  //   XOR
  //   SRL
  //   SRA
  //   OR
  //   AND
endmodule

module ALU_reference_3 (
  input  [2:0] Funct3,
  input  I,
  input  [1:0] ALU_op,
  input  [31:0] Y,
  input  [31:0] X,
  output [31:0] out_6,
  output Branch
);

  wire and_2_out, or_1_out;
  wire [2:0] and_1_out, multiplexer_1_out, rom_1_data, rom_3_data, rom_4_data, rom_5_data, rom_6_data;
  wire [7:0] rom_1_data_2;
  wire [7:2] rom_7_data;
  wire [7:7] rom_2_data, rom_3_data_2, rom_4_data_2, rom_5_data_2, rom_6_data_2;

  or or_1 (or_1_out, ALU_op[0], ALU_op[1]);
  and and_1 (and_1_out[1], I, ~or_1_out);  // AND_Gate
  Multiplexer #(.enable("false"), .width(3)) multiplexer_1 (
    .in0(Funct3), .in1(3'b000), .out(multiplexer_1_out), .sel(and_2_out));
  and and_2 (and_2_out, ALU_op[0], ~ALU_op[1]);  // AND_Gate
  ROM #(.addrWidth(17)) rom_1 (
    .addr({1'b0, Y[4:0], X[4:0], multiplexer_1_out, 1'b1, and_1_out[1], 1'b0}),
    .data({rom_1_data_2[7], rom_1_data[2], rom_1_data[0], out_6[4:1], rom_1_data_2[0]}));
  ROM #(.addrWidth(17)) rom_2 (
    .addr({1'b0, Y[9:5], X[9:5], multiplexer_1_out, rom_1_data[2], and_1_out[1], rom_1_data[0]}),
    .data({rom_2_data[7], and_1_out[2], and_1_out[0], out_6[9:5]}));
  ROM #(.addrWidth(17)) rom_3 (
    .addr({1'b0, Y[14:10], X[14:10], multiplexer_1_out, and_1_out}),
    .data({rom_3_data_2[7], rom_3_data[2], rom_3_data[0], out_6[14:10]}));
  ROM #(.addrWidth(17)) rom_4 (
    .addr({1'b0, Y[19:15], X[19:15], multiplexer_1_out, rom_3_data[2], and_1_out[1], rom_3_data[0]}),
    .data({rom_4_data_2[7], rom_4_data[2], rom_4_data[0], out_6[19:15]}));
  ROM #(.addrWidth(17)) rom_5 (
    .addr({1'b0, Y[24:20], X[24:20], multiplexer_1_out, rom_4_data[2], and_1_out[1], rom_4_data[0]}),
    .data({rom_5_data_2[7], rom_5_data[2], rom_5_data[0], out_6[24:20]}));
  ROM #(.addrWidth(17)) rom_6 (
    .addr({1'b0, Y[29:25], X[29:25], multiplexer_1_out, rom_5_data[2], and_1_out[1], rom_5_data[0]}),
    .data({rom_6_data_2[7], rom_6_data[2], rom_6_data[0], out_6[29:25]}));
  ROM #(.addrWidth(17)) rom_7 (
    .addr({4'b0000, Y[31:30], 3'b000, X[31:30], multiplexer_1_out, rom_6_data[2], and_1_out[1], rom_6_data[0]}),
    .data({rom_7_data[7], Branch, rom_7_data[5:2], out_6[31:30]}));
  or or_2 (out_6[0], rom_7_data[5], rom_1_data_2[0]);

  // Notes on the sheet:
  //   Funct3
  //   i
  //   contents of rom_1 (hex, n*v repeats v):
  //   compressed eJyl3dFyIjuQBNB3vqKf75OBBuzPsT3m/z/hUplVKpVQFYogYmOdu5ceqz1uziRqtT624/axne/b
  //   /rHtR/nft/vh67+P7fSxxf91mP3/jqfHS/f/Hod1aTvJH3rQr9sn/p/X/yQd8X8dLDxeccarHl8P
  //   8rV/7Yn/l4XDedvxav166F97ttdq2LfLYccrL3h1e60cZa/VcNmu8qqDfg1juNh4GR6vuOFVj68H
  //   +dq/9mp/LsPhtn3i1fo1jPdmr7WwfR0+8covvLof76e9VsPX9i2vOujXMI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
  //   contents of rom_2 (hex, n*v repeats v):
  //   compressed eJytnU1iI6uyhOe1ihrfkfVn2cux29b+l3CVEZFAZpEcDTx4R3FfFy2wBV8HoYS3/bS/7ZfHfn3b
  //   ryf77/2xXf/3/B//e+q3/Tz8Z4v/c/j/tQYH0f+u037Gez1fN3v9wP/z/X+mTvxfLrbzfsHTet3G
  //   Z8/+rMRlv24XPHnF0+3ZZ6uLPytx3W/21KbX0Icr39rF84l3PPV83ex1fPbmfy/F9r7f8bReQ3/f
  //   /VmJ+/6x3fHkB54e+3v3Z13sn/bUptfQhw/vL8XziS889Xzd7HV89tP/Xo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
  //   contents of rom_3 (hex, n*v repeats v):
  //   compressed eJytnU1iI6uyhOe1ihrfkfVn2cux29b+l3CVEZFAZpEcDTx4R3FfFy2wBV8HoYS3/bS/7ZfHfn3b
  //   ryf77/2xXf/3/B//e+q3/Tz8Z4v/c/j/tQYH0f+u037Gez1fN3v9wP/z/X+mTvxfLrbzfsHTet3G
  //   Z8/+rMRlv24XPHnF0+3ZZ6uLPytx3W/21KbX0Icr39rF84l3PPV83ex1fPbmfy/F9r7f8bReQ3/f
  //   /VmJ+/6x3fHkB54e+3v3Z13sn/bUptfQhw/vL8XziS889Xzd7HV89tP/Xo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
  //   contents of rom_4 (hex, n*v repeats v):
  //   compressed eJytnU1iI6uyhOe1ihrfkfVn2cux29b+l3CVEZFAZpEcDTx4R3FfFy2wBV8HoYS3/bS/7ZfHfn3b
  //   ryf77/2xXf/3/B//e+q3/Tz8Z4v/c/j/tQYH0f+u037Gez1fN3v9wP/z/X+mTvxfLrbzfsHTet3G
  //   Z8/+rMRlv24XPHnF0+3ZZ6uLPytx3W/21KbX0Icr39rF84l3PPV83ex1fPbmfy/F9r7f8bReQ3/f
  //   /VmJ+/6x3fHkB54e+3v3Z13sn/bUptfQhw/vL8XziS889Xzd7HV89tP/Xo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
  //   contents of rom_5 (hex, n*v repeats v):
  //   compressed eJytnU1iI6uyhOe1ihrfkfVn2cux29b+l3CVEZFAZpEcDTx4R3FfFy2wBV8HoYS3/bS/7ZfHfn3b
  //   ryf77/2xXf/3/B//e+q3/Tz8Z4v/c/j/tQYH0f+u037Gez1fN3v9wP/z/X+mTvxfLrbzfsHTet3G
  //   Z8/+rMRlv24XPHnF0+3ZZ6uLPytx3W/21KbX0Icr39rF84l3PPV83ex1fPbmfy/F9r7f8bReQ3/f
  //   /VmJ+/6x3fHkB54e+3v3Z13sn/bUptfQhw/vL8XziS889Xzd7HV89tP/Xo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
  //   contents of rom_6 (hex, n*v repeats v):
  //   compressed eJytnU1iI6uyhOe1ihrfkfVn2cux29b+l3CVEZFAZpEcDTx4R3FfFy2wBV8HoYS3/bS/7ZfHfn3b
  //   ryf77/2xXf/3/B//e+q3/Tz8Z4v/c/j/tQYH0f+u037Gez1fN3v9wP/z/X+mTvxfLrbzfsHTet3G
  //   Z8/+rMRlv24XPHnF0+3ZZ6uLPytx3W/21KbX0Icr39rF84l3PPV83ex1fPbmfy/F9r7f8bReQ3/f
  //   /VmJ+/6x3fHkB54e+3v3Z13sn/bUptfQhw/vL8XziS889Xzd7HV89tP/Xo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
  //   contents of rom_7 (hex, n*v repeats v):
  //   compressed eJytnUuW87iOhOdchcZ39MvPzOWk0/b+l9BGBAACfEgud57TXYlbZUqmJeoTAALxb1mXf8v6XE7/
  //   ltMq/zw/y+l/r//xv5f9bzmEf5T8P8O/8wGdUY+1LgeeazkU+fuFf3n5n1gr/5cZ5bAc8Wn9W/S/
  //   HuQfGHlQ48CBx3LCJ48L/+Ig8fNHNY78/Gk5Y8TrL0bgX75O285ORr1mcJIZnOrkXh/nkPNyKWcc
  //   5YIj+ZxeJz/bnNS4LFf5VNG/SzenS6Fx4X+6Ll/45LXwb/f5K77d1/+u+p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
endmodule

module Program_Counter_1 (
  input  [31:0] in,
  input  Enable,
  input  Clock,
  input  Clear,
  output [31:0] out
);

  Register #(.width(32)) register_1 (.D(in), .en(Enable), .Q(out), .clk(Clock), .clr(Clear));
endmodule

module Program_counter_2 (
  input  SRC1,
  input  CLK,
  input  T_BRCH,
  input  SRC0,
  input  BRCH,
  input  RST,
  input  [31:0] Y,
  input  [31:0] OUT_in,
  output [31:0] X,
  output [31:0] OUT
);

  wire and_1_out, and_2_out, and_3_out, not_1_out, not_2_out, not_3_out, or_1_out, PC_Clear_out;
  wire [31:0] pc_adder_1_out_5;

  and and_1 (and_1_out, ~T_BRCH, SRC0);  // AND_Gate
  and and_2 (and_2_out, BRCH, T_BRCH);
  or or_1 (or_1_out, and_1_out, and_2_out);
  PC_Adder pc_adder_1 (.out_5(pc_adder_1_out_5), .Y(Y), .X(X), .Mode(or_1_out), .Rst(RST));
  assign OUT = not_1_out ? pc_adder_1_out_5 : 32'bz;  // Controlled_Buffer controlled_buffer_1
  not not_1 (not_1_out, and_3_out);
  and and_3 (and_3_out, SRC1, SRC1);
  Button PC_Clear (.out(PC_Clear_out));
  assign OUT = not_2_out ? OUT_in : 32'bz;  // Controlled_Buffer controlled_buffer_2
  not not_2 (not_2_out, not_3_out);
  not not_3 (not_3_out, SRC1);
  Program_Counter_1 program_counter_1_1 (.out(X), .Enable(1'b1), .Clock(CLK), .in(OUT), .Clear(PC_Clear_out));

  // Other names for the same wires on the sheet: branch = BRCH; PC_Source = SRC0; PC_Source_1 = SRC1;
  //   Take_branch = T_BRCH

  // Notes on the sheet:
  //   Inputs
  //   Circuit
  //   PROGRAM COUNTER
  //   Outputs
endmodule

module PC_Adder (
  input  [31:0] Y,
  input  [31:0] X,
  input  Mode,
  input  Rst,
  output [31:0] out_5
);

  wire [0:0] rom_1_data, rom_2_data, rom_3_data, rom_4_data;
  wire [7:4] rom_5_data;

  ROM #(.addrWidth(17)) rom_1 (.addr({Rst, Y[6:0], X[6:0], Mode, 1'b0}), .data({rom_1_data[0], out_5[6:0]}));
  ROM #(.addrWidth(17)) rom_2 (
    .addr({Rst, Y[13:7], X[13:7], Mode, rom_1_data[0]}), .data({rom_2_data[0], out_5[13:7]}));
  ROM #(.addrWidth(17)) rom_3 (
    .addr({Rst, Y[20:14], X[20:14], Mode, rom_2_data[0]}), .data({rom_3_data[0], out_5[20:14]}));
  ROM #(.addrWidth(17)) rom_4 (
    .addr({Rst, Y[27:21], X[27:21], Mode, rom_3_data[0]}), .data({rom_4_data[0], out_5[27:21]}));
  ROM #(.addrWidth(17)) rom_5 (
    .addr({Rst, 3'b000, Y[31:28], 3'b000, X[31:28], Mode, rom_4_data[0]}), .data({rom_5_data, out_5[31:28]}));

  // Notes on the sheet:
  //   contents of rom_1 (hex, n*v repeats v):
  //   compressed eJxk3VuS29YBRdF/joJDsN7ScCTbmv8QQux1btoNVcUMEgJsEsBdtYNXPj+/PP96fni9fn29fnx8
  //   fX57fnx+er1+f71+fnx//nh+fr374/nzmufx8/nrec3z6/n3Nc/j7+c/z2uef57/XvM8/n3+fl7z
  //   /H5++Oua6fH6tw8fntdsr3/78PGa8fH6tw+fntesr3/78LmZH69///DlafZr4qsFHtfEt6dFronv
  //   FnpcEz+eW+o18dNSj2vi13NLvSb+ttTjmvjnuaVeE/9a6nFN/H5uqd/Pj3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
  //   contents of rom_2 (hex, n*v repeats v):
  //   compressed eJxk3VmO3EajbtF3joJDUN8MR9IvzX8IJ2Ovj3V9UUBWOODsScbCtiWFPtwf7w+vn4/3p/Nzfbo/
  //   3+fn8/3l/Fxf7q/3+fl6fzs/17f7+31+vt8/zs/14/55n5+f96/zc/26f9/n5/f95/xcf+7/3efn
  //   f/ff83P9vf/d5+ff/fFDw/X658eP98bX7ZPxOpPP98bX7YvxOpOv98bX7ZvxOpPv98bX7YfxOpOf
  //   98bX7ZfxOpPf98bX7Y/xOpP/3Rtft7/G60z+3Rv/3Z8+GK/X5NPHe+Pr9s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
  //   contents of rom_3 (hex, n*v repeats v):
  //   compressed eJxk3VmO3EajbtF3joJDUN8MR9IvzX8IJ2Ovj3V9UUBWOODsScbCtiWFPtwf7w+vn4/3p/Nzfbo/
  //   3+fn8/3l/Fxf7q/3+fl6fzs/17f7+31+vt8/zs/14/55n5+f96/zc/26f9/n5/f95/xcf+7/3efn
  //   f/ff83P9vf/d5+ff/fFDw/X658eP98bX7ZPxOpPP98bX7YvxOpOv98bX7ZvxOpPv98bX7YfxOpOf
  //   98bX7ZfxOpPf98bX7Y/xOpP/3Rtft7/G60z+3Rv/3Z8+GK/X5NPHe+Pr9s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
  //   contents of rom_4 (hex, n*v repeats v):
  //   compressed eJxk3VmO3EajbtF3joJDUN8MR9IvzX8IJ2Ovj3V9UUBWOODsScbCtiWFPtwf7w+vn4/3p/Nzfbo/
  //   3+fn8/3l/Fxf7q/3+fl6fzs/17f7+31+vt8/zs/14/55n5+f96/zc/26f9/n5/f95/xcf+7/3efn
  //   f/ff83P9vf/d5+ff/fFDw/X658eP98bX7ZPxOpPP98bX7YvxOpOv98bX7ZvxOpPv98bX7YfxOpOf
  //   98bX7ZfxOpPf98bX7Y/xOpP/3Rtft7/G60z+3Rv/3Z8+GK/X5NPHe+Pr9s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
  //   contents of rom_5 (hex, n*v repeats v):
  //   compressed eJxk3VmO3EajbtF3joJDUN8MR9IvzX8IJ2Ovj3V9UUBWOODsScbCtiWFPtwf7w+vn4/3p/Nzfbo/
  //   3+fn8/3l/Fxf7q/3+fl6fzs/17f7+31+vt8/zs/14/55n5+f96/zc/26f9/n5/f95/xcf+7/3efn
  //   f/ff83P9vf/d5+ff/fFDw/X658eP98bX7ZPxOpPP98bX7YvxOpOv98bX7ZvxOpPv98bX7YfxOpOf
  //   98bX7ZfxOpPf98bX7Y/xOpP/3Rtft7/G60z+3Rv/3Z8+GK/X5NPHe+Pr9s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
endmodule

module Instruction_memory (
  input  [31:0] in,
  input  [7:0] in_2,
  input  [7:0] in_3,
  input  [7:0] in_4,
  input  [7:0] in_5,
  output [18:0] out_6,
  output [31:0] out_7
);


  assign out_6 = in[18:0];
  assign out_7 = {in_2, in_3, in_4, in_5};
endmodule

module Data_memory (
  input  Load,
  input  Store,
  input  Clock,
  input  [31:0] Data,
  input  [2:0] Funct3,
  input  [31:0] Adress,
  output [31:0] out_7,
  output Exception,
  output out_9,
  output [3:0] STR_SEL,
  output [10:0] GPU_ADDR,
  output STR,
  output [31:0] GPU_DATA
);

  wire and_1_out, and_2_out, and_3_out, and_4_out, and_5_out, and_6_out, and_7_out, and_8_out, and_9_out,
       and_12_out, and_13_out, and_19_out, and_24_out, and_25_out, and_26_out, and_27_out, and_28_out,
       and_29_out, and_33_out, and_37_out, and_42_out, and_43_out, and_44_out, and_45_out, and_47_out,
       and_48_out, and_49_out, and_50_out, B, B0, B1, B2, B3, BO0, BO1, BO2, BO3, button_3_out,
       counter_2_carry, decoder_1_out0, decoder_1_out1, decoder_1_out2, decoder_1_out3, decoder_1_out6,
       decoder_1_out7, decoder_2_out0, decoder_2_out1, decoder_2_out2, decoder_2_out3, decoder_2_out4,
       decoder_2_out5, decoder_2_out6, decoder_2_out7, decoder_2_out8, decoder_2_out9, decoder_2_out10,
       decoder_2_out11, decoder_2_out12, decoder_2_out13, decoder_2_out14, decoder_2_out15, decoder_3_out0,
       decoder_3_out1, decoder_3_out2, decoder_3_out3, decoder_3_out4, decoder_3_out5, decoder_3_out6,
       decoder_3_out7, decoder_3_out8, decoder_3_out9, decoder_3_out10, decoder_3_out11, decoder_3_out12,
       decoder_3_out13, decoder_3_out14, decoder_3_out15, decoder_4_out0, decoder_4_out1, decoder_4_out2,
       decoder_4_out3, decoder_4_out4, decoder_4_out5, decoder_4_out6, decoder_4_out7, decoder_5_out0,
       decoder_5_out1, decoder_5_out2, decoder_5_out3, decoder_5_out4, decoder_5_out5, decoder_5_out6,
       decoder_5_out7, decoder_5_out8, decoder_5_out9, decoder_5_out10, decoder_5_out11, decoder_5_out12,
       decoder_5_out13, decoder_5_out14, decoder_5_out15, G1, G2, G3, G5, G7, G8, G9, G10, H, H0, H1, H3,
       HO0, HO1, HO2, HO3, in2_ac, iS4Clk, iS5Clk, Load_BYPASS, multiplexer_2_out, multiplexer_3_out,
       multiplexer_4_out, nand_1_out, nand_2_out, nand_4_out, nand_5_out, nand_6_out, nand_7_out, nand_8_out,
       nand_9_out, nand_10_out, nand_11_out, nand_12_out, not_18_out, not_19_out, not_20_out, not_21_out,
       not_22_out, not_23_out, not_24_out, not_26_out, not_27_out, not_28_out, not_29_out, not_30_out,
       not_31_out, not_32_out, not_33_out, not_34_out, not_35_out, not_36_out, not_37_out, not_38_out,
       not_55_out, not_56_out, not_57_out, not_58_out, not_59_out, not_60_out, not_61_out, not_70_out,
       not_71_out, not_72_out, not_73_out, not_74_out, not_75_out, not_76_out, not_77_out, not_78_out,
       not_79_out, not_80_out, not_81_out, not_82_out, not_83_out, not_84_out, not_85_out, not_86_out,
       or_2_out, SR_input_en, Store_R0, Store_R1, Store_R2, Store_R3, Store_VR0, Store_VR1, Store_VR2,
       Store_VR3, to_SP, to_SRAM, to_VRAM, W1, W2, W3, WO0, WO1, WO2, WO3;
  wire [7:0] bit_extender_1_out, bit_extender_2_out, BYTE_0_2_data, BYTE_1_2_data, BYTE_2_2_data,
       BYTE_3_2_data, in1, in2, iS4, iS5, not_25_out, S0, S1, S2, S3, S6, S7;
  wire [8:0] counter_2_q;
  wire [10:0] GPU_ADR, multiplexer_1_out;
  wire [23:0] rgb_video_1_p6;

  // NOT_Gate not_1 is placed but not wired
  // Probe on S0
  // Probe on S1
  // Probe on S2
  // Probe on S3
  // Probe on in1
  // Probe on in2
  // Probe on S6
  // Probe on S7
  and and_1 (and_1_out, Store, to_SRAM);
  and and_2 (and_2_out, Clock, Store);
  and and_3 (and_3_out, to_SP, and_2_out);
  Decoder #(.select(4)) decoder_1 (
    .out0(decoder_1_out0), .out1(decoder_1_out1), .out2(decoder_1_out2), .out3(decoder_1_out3),
    .out6(decoder_1_out6), .out7(decoder_1_out7), .sel(Adress[3:0]), .en(and_3_out));  // open: out4, out5, out8, out9, out10, out11, out12, out13, out14, out15
  and and_4 (and_4_out, to_SP, Load);
  Decoder #(.select(4)) decoder_2 (
    .out0(decoder_2_out0), .out1(decoder_2_out1), .out2(decoder_2_out2), .out3(decoder_2_out3),
    .out4(decoder_2_out4), .out5(decoder_2_out5), .out6(decoder_2_out6), .out7(decoder_2_out7),
    .out8(decoder_2_out8), .out9(decoder_2_out9), .out10(decoder_2_out10), .out11(decoder_2_out11),
    .out12(decoder_2_out12), .out13(decoder_2_out13), .out14(decoder_2_out14), .out15(decoder_2_out15),
    .sel(Adress[3:0]), .en(and_4_out));
  nand nand_1 (nand_1_out, W3, W2, W1, H3, H1);
  and and_5 (and_5_out, and_1_out, ~Clock);  // AND_Gate
  LED led_1 (.in(nand_1_out));
  // NOT_Gate not_2 has open pins: in=decoder_2_out0, out=open
  // NOT_Gate not_3 has open pins: in=decoder_2_out1, out=open
  // NOT_Gate not_4 has open pins: in=decoder_2_out2, out=open
  // NOT_Gate not_5 has open pins: in=decoder_2_out3, out=open
  not not_6 (out_9, decoder_2_out4);
  not not_7 (in2_ac, decoder_2_out5);
  // NOT_Gate not_8 has open pins: in=decoder_2_out6, out=open
  // NOT_Gate not_9 has open pins: in=decoder_2_out7, out=open
  // NOT_Gate not_10 has open pins: in=decoder_2_out8, out=open
  // NOT_Gate not_11 has open pins: in=decoder_2_out9, out=open
  // NOT_Gate not_12 has open pins: in=decoder_2_out10, out=open
  // NOT_Gate not_13 has open pins: in=decoder_2_out11, out=open
  // NOT_Gate not_14 has open pins: in=decoder_2_out12, out=open
  // NOT_Gate not_15 has open pins: in=decoder_2_out13, out=open
  // NOT_Gate not_16 has open pins: in=decoder_2_out14, out=open
  // NOT_Gate not_17 has open pins: in=decoder_2_out15, out=open
  and and_6 (and_6_out, nand_1_out, and_5_out);
  or or_1 (Exception, and_6_out, and_7_out);
  Button button_1 (.out(iS4Clk));
  // DipSwitch dipswitch_1: pin names not known
  Button button_2 (.out(iS5Clk));
  // DipSwitch dipswitch_2: pin names not known
  nand nand_2 (nand_2_out, WO3, WO2, WO1, HO3, HO1);
  and and_7 (and_7_out, nand_2_out, and_9_out);
  LED led_2 (.in(nand_2_out));
  Register SReg_3 (.D(GPU_DATA[31:24]), .en(1'b1), .Q(S3), .clk(decoder_1_out3), .clr(1'b0));
  Register SReg_7 (.D(GPU_DATA[31:24]), .en(1'b1), .Q(S7), .clk(decoder_1_out7));  // open: clr
  assign GPU_DATA[7:0] = not_18_out ? in1 : 8'bz;  // Controlled_Buffer controlled_buffer_1
  not not_18 (not_18_out, out_9);
  assign GPU_DATA[7:0] = not_19_out ? in2 : 8'bz;  // Controlled_Buffer controlled_buffer_2
  not not_19 (not_19_out, in2_ac);
  nand nand_3 (SR_input_en, Load, to_SP);
  and and_8 (and_8_out, Load, to_SRAM);
  and and_9 (and_9_out, and_8_out, ~Clock);  // AND_Gate
  Register SReg_2 (.D(GPU_DATA[23:16]), .en(1'b1), .Q(S2), .clk(decoder_1_out2), .clr(1'b0));
  Register SReg_6 (.D(GPU_DATA[23:16]), .en(1'b1), .Q(S6), .clk(decoder_1_out6));  // open: clr
  and and_10 (G1, G3, B0, H0);
  and and_11 (G2, G3, H0);
  Register SReg_1 (.D(GPU_DATA[15:8]), .en(1'b1), .Q(S1), .clk(decoder_1_out1), .clr(1'b0));
  Register SReg_5 (.D(iS5), .en(1'b1), .Q(in2), .clk(iS5Clk));  // open: clr
  assign GPU_DATA[7:0] = not_20_out ? Data[7:0] : 8'bz;  // Controlled_Buffer controlled_buffer_3
  not not_20 (not_20_out, G1);
  not not_21 (not_21_out, G2);
  not not_22 (not_22_out, G1);
  nand nand_4 (nand_4_out, G2, B1);
  nand nand_5 (nand_5_out, G3, G5);
  nand nand_6 (nand_6_out, G3, B3, G7);
  and and_12 (and_12_out, Store, to_SRAM);
  and and_13 (and_13_out, and_12_out, Clock);
  assign GPU_DATA[15:8] = not_21_out ? Data[15:8] : 8'bz;  // Controlled_Buffer controlled_buffer_4
  assign GPU_DATA[23:16] = not_23_out ? Data[23:16] : 8'bz;  // Controlled_Buffer controlled_buffer_5
  assign GPU_DATA[31:24] = not_24_out ? Data[31:24] : 8'bz;  // Controlled_Buffer controlled_buffer_6
  not not_23 (not_23_out, G3);
  not not_24 (not_24_out, G3);
  and and_14 (Store_R0, and_13_out, not_22_out);
  and and_15 (Store_R1, and_13_out, nand_4_out);
  and and_16 (Store_R2, and_13_out, nand_5_out);
  and and_17 (Store_R3, and_13_out, nand_6_out);
  Register SReg_0 (.D(GPU_DATA[7:0]), .en(1'b1), .Q(S0), .clk(decoder_1_out0), .clr(1'b0));
  Register SReg_4 (.D(iS4), .en(1'b1), .Q(in1), .clk(iS4Clk));  // open: clr
  assign not_25_out = ~S0;  // NOT_Gate not_25, 8 bits wide
  assign GPU_DATA[15:8] = not_26_out ? Data[7:0] : 8'bz;  // Controlled_Buffer controlled_buffer_7
  assign GPU_DATA[23:16] = not_27_out ? Data[7:0] : 8'bz;  // Controlled_Buffer controlled_buffer_8
  not not_26 (not_26_out, B1);
  not not_27 (not_27_out, G5);
  not not_28 (not_28_out, B3);
  and and_18 (G5, B2, G7);
  Pull_Resistor pull_resistor_1 (.node(GPU_DATA[31:24]));
  assign GPU_DATA[31:24] = not_28_out ? Data[7:0] : 8'bz;  // Controlled_Buffer controlled_buffer_9
  assign GPU_DATA[31:24] = not_29_out ? Data[15:8] : 8'bz;  // Controlled_Buffer controlled_buffer_10
  not not_29 (not_29_out, G7);
  not not_30 (not_30_out, G1);
  nand nand_7 (nand_7_out, G2, B1);
  nand nand_8 (nand_8_out, G3, G5);
  nand nand_9 (nand_9_out, G3, B3, G7);
  and and_19 (and_19_out, Store, to_VRAM);
  _7_Segment_Display u_7_segment_display_1 (
    .g(not_25_out[6]), .f(not_25_out[5]), .a(not_25_out[0]), .b(not_25_out[1]), .e(not_25_out[4]),
    .d(not_25_out[3]), .c(not_25_out[2]), .dp(not_25_out[7]));
  Pull_Resistor pull_resistor_2 (.node(GPU_DATA[23:16]));
  Pull_Resistor pull_resistor_3 (.node(GPU_DATA[15:8]));
  Pull_Resistor pull_resistor_4 (.node(GPU_DATA[7:0]));
  and and_20 (Store_VR0, and_24_out, not_30_out);
  and and_21 (Store_VR1, and_24_out, nand_7_out);
  and and_22 (Store_VR2, and_24_out, nand_8_out);
  and and_23 (Store_VR3, and_24_out, nand_9_out);
  and and_24 (and_24_out, and_19_out, Clock);
  not not_31 (not_31_out, Store_R0);
  not not_32 (not_32_out, not_31_out);
  and and_25 (and_25_out, to_SRAM, Load);
  not not_33 (not_33_out, Store_R1);
  not not_34 (not_34_out, not_33_out);
  not not_35 (not_35_out, Store_R2);
  not not_36 (not_36_out, not_35_out);
  not not_37 (not_37_out, Store_R3);
  not not_38 (not_38_out, not_37_out);
  and and_26 (and_26_out, not_32_out, Store_R0);
  and and_27 (and_27_out, not_34_out, Store_R1);
  and and_28 (and_28_out, not_36_out, Store_R2);
  and and_29 (and_29_out, not_38_out, Store_R3);
  Decoder #(.select(4)) decoder_3 (
    .out0(decoder_3_out0), .out1(decoder_3_out1), .out2(decoder_3_out2), .out3(decoder_3_out3),
    .out4(decoder_3_out4), .out5(decoder_3_out5), .out6(decoder_3_out6), .out7(decoder_3_out7),
    .out8(decoder_3_out8), .out9(decoder_3_out9), .out10(decoder_3_out10), .out11(decoder_3_out11),
    .out12(decoder_3_out12), .out13(decoder_3_out13), .out14(decoder_3_out14), .out15(decoder_3_out15),
    .sel({Funct3[1:0], Adress[1:0]}), .en(Store));
  Counter counter_1 (.clk(Store_R0));  // open: load, D, count, Q, carry, clr
  RAM #(.addrWidth(17), .databus("bidir")) BYTE_0 (.addr(Adress[18:2]), .data(GPU_DATA[7:0]));  // open: we, oe, clk
  RAM #(.addrWidth(17), .databus("bidir")) BYTE_1 (.addr(Adress[18:2]), .data(GPU_DATA[15:8]));  // open: we, oe, clk
  RAM #(.addrWidth(17), .databus("bidir")) BYTE_2 (.addr(Adress[18:2]), .data(GPU_DATA[23:16]));  // open: we, oe, clk
  RAM #(.addrWidth(17), .databus("bidir")) BYTE_3 (.addr(Adress[18:2]), .data(GPU_DATA[31:24]));  // open: we, oe, clk
  not not_39 (B0, decoder_3_out0);
  not not_40 (B1, decoder_3_out1);
  not not_41 (B2, decoder_3_out2);
  not not_42 (B3, decoder_3_out3);
  not not_43 (H0, decoder_3_out4);
  not not_44 (H1, decoder_3_out5);
  not not_45 (G7, decoder_3_out6);
  not not_46 (H3, decoder_3_out7);
  not not_47 (G3, decoder_3_out8);
  not not_48 (W1, decoder_3_out9);
  not not_49 (W2, decoder_3_out10);
  not not_50 (W3, decoder_3_out11);
  // NOT_Gate not_51 has open pins: in=decoder_3_out12, out=open
  // NOT_Gate not_52 has open pins: in=decoder_3_out13, out=open
  // NOT_Gate not_53 has open pins: in=decoder_3_out14, out=open
  // NOT_Gate not_54 has open pins: in=decoder_3_out15, out=open
  and and_30 (to_VRAM, Adress[30], not_56_out);
  and and_31 (to_SP, not_55_out, Adress[31]);
  not not_55 (not_55_out, Adress[30]);
  and and_32 (to_SRAM, not_55_out, not_56_out);
  not not_56 (not_56_out, Adress[31]);
  and and_33 (and_33_out, WO0, BO0, HO0);
  and and_34 (G9, WO0, HO0);
  not not_57 (not_57_out, G8);
  and and_35 (G8, SR_input_en, and_33_out);
  not not_58 (not_58_out, G1);
  nand nand_10 (nand_10_out, G2, B1);
  nand nand_11 (nand_11_out, G3, G5);
  nand nand_12 (nand_12_out, G3, B3, G7);
  and and_36 (STR, Store, to_VRAM);
  assign out_7[7:0] = not_57_out ? GPU_DATA[7:0] : 8'bz;  // Controlled_Buffer controlled_buffer_11
  assign out_7[15:8] = not_59_out ? GPU_DATA[15:8] : 8'bz;  // Controlled_Buffer controlled_buffer_12
  assign out_7[23:16] = not_60_out ? GPU_DATA[23:16] : 8'bz;  // Controlled_Buffer controlled_buffer_13
  assign out_7[31:24] = not_61_out ? GPU_DATA[31:24] : 8'bz;  // Controlled_Buffer controlled_buffer_14
  not not_59 (not_59_out, G9);
  not not_60 (not_60_out, WO0);
  not not_61 (not_61_out, WO0);
  Decoder #(.select(3)) decoder_4 (
    .out0(decoder_4_out0), .out1(decoder_4_out1), .out2(decoder_4_out2), .out3(decoder_4_out3),
    .out4(decoder_4_out4), .out5(decoder_4_out5), .out6(decoder_4_out6), .out7(decoder_4_out7), .sel(Funct3),
    .en(Load));
  and and_37 (and_37_out, to_VRAM, Load);
  and and_38 (STR_SEL[0], STR, not_58_out);
  and and_39 (STR_SEL[1], STR, nand_10_out);
  and and_40 (STR_SEL[2], STR, nand_11_out);
  and and_41 (STR_SEL[3], STR, nand_12_out);
  not not_62 (B, decoder_4_out0);
  not not_63 (H, decoder_4_out1);
  // NOT_Gate not_64 has open pins: in=decoder_4_out2, out=open
  // NOT_Gate not_65 has open pins: in=decoder_4_out3, out=open
  // NOT_Gate not_66 has open pins: in=decoder_4_out4, out=open
  // NOT_Gate not_67 has open pins: in=decoder_4_out5, out=open
  // NOT_Gate not_68 has open pins: in=decoder_4_out6, out=open
  // NOT_Gate not_69 has open pins: in=decoder_4_out7, out=open
  not not_70 (not_70_out, Store_VR0);
  not not_71 (not_71_out, not_70_out);
  and and_42 (and_42_out, not_71_out, Store_VR0);
  not not_72 (not_72_out, Store_VR1);
  not not_73 (not_73_out, not_72_out);
  and and_43 (and_43_out, not_73_out, Store_VR1);
  not not_74 (not_74_out, Store_VR2);
  not not_75 (not_75_out, not_74_out);
  and and_44 (and_44_out, not_75_out, Store_VR2);
  not not_76 (not_76_out, Store_VR3);
  not not_77 (not_77_out, not_76_out);
  and and_45 (and_45_out, not_77_out, Store_VR3);
  assign out_7[7:0] = not_78_out ? GPU_DATA[15:8] : 8'bz;  // Controlled_Buffer controlled_buffer_15
  assign out_7[7:0] = not_79_out ? GPU_DATA[23:16] : 8'bz;  // Controlled_Buffer controlled_buffer_16
  not not_78 (not_78_out, BO1);
  not not_79 (not_79_out, G10);
  not not_80 (not_80_out, BO3);
  and and_46 (G10, BO2, HO2);
  Multiplexer #(.enable("false"), .width(11)) multiplexer_1 (
    .in0(GPU_ADR), .in1(Adress[12:2]), .out(multiplexer_1_out), .sel(to_VRAM));
  or or_2 (or_2_out, and_37_out, Load_BYPASS);
  assign out_7[7:0] = not_80_out ? GPU_DATA[31:24] : 8'bz;  // Controlled_Buffer controlled_buffer_17
  assign out_7[15:8] = not_81_out ? GPU_DATA[31:24] : 8'bz;  // Controlled_Buffer controlled_buffer_18
  not not_81 (not_81_out, HO2);
  RAM #(.addrWidth(11), .databus("bidir")) BYTE_0_2 (
    .addr(multiplexer_1_out), .data(BYTE_0_2_data));  // open: we, oe, clk
  RAM #(.addrWidth(11), .databus("bidir")) BYTE_1_2 (
    .addr(multiplexer_1_out), .data(BYTE_1_2_data));  // open: we, oe, clk
  RAM #(.addrWidth(11), .databus("bidir")) BYTE_2_2 (
    .addr(multiplexer_1_out), .data(BYTE_2_2_data));  // open: we, oe, clk
  RAM #(.addrWidth(11), .databus("bidir")) BYTE_3_2 (
    .addr(multiplexer_1_out), .data(BYTE_3_2_data));  // open: we, oe, clk
  assign bit_extender_1_out = {{7{out_7[7]}}, out_7[7]};  // Bit_Extender bit_extender_1
  not not_82 (not_82_out, B);
  assign out_7[15:8] = not_82_out ? bit_extender_1_out : 8'bz;  // Controlled_Buffer controlled_buffer_19
  not not_83 (not_83_out, B);
  assign out_7[23:16] = not_83_out ? bit_extender_1_out : 8'bz;  // Controlled_Buffer controlled_buffer_20
  not not_84 (not_84_out, B);
  assign out_7[31:24] = not_84_out ? bit_extender_1_out : 8'bz;  // Controlled_Buffer controlled_buffer_21
  assign bit_extender_2_out = {{7{out_7[15]}}, out_7[15]};  // Bit_Extender bit_extender_2
  // Probe on bit_extender_1_out
  assign out_7[23:16] = not_85_out ? bit_extender_2_out : 8'bz;  // Controlled_Buffer controlled_buffer_22
  assign out_7[31:24] = not_86_out ? bit_extender_2_out : 8'bz;  // Controlled_Buffer controlled_buffer_23
  not not_85 (not_85_out, H);
  not not_86 (not_86_out, H);
  Decoder #(.select(4)) decoder_5 (
    .out0(decoder_5_out0), .out1(decoder_5_out1), .out2(decoder_5_out2), .out3(decoder_5_out3),
    .out4(decoder_5_out4), .out5(decoder_5_out5), .out6(decoder_5_out6), .out7(decoder_5_out7),
    .out8(decoder_5_out8), .out9(decoder_5_out9), .out10(decoder_5_out10), .out11(decoder_5_out11),
    .out12(decoder_5_out12), .out13(decoder_5_out13), .out14(decoder_5_out14), .out15(decoder_5_out15),
    .sel({Funct3[1:0], Adress[1:0]}), .en(and_47_out));
  and and_47 (and_47_out, ~to_SP, Load);  // AND_Gate
  not not_87 (BO0, decoder_5_out0);
  not not_88 (BO1, decoder_5_out1);
  not not_89 (BO2, decoder_5_out2);
  not not_90 (BO3, decoder_5_out3);
  not not_91 (HO0, decoder_5_out4);
  not not_92 (HO1, decoder_5_out5);
  not not_93 (HO2, decoder_5_out6);
  not not_94 (HO3, decoder_5_out7);
  not not_95 (WO0, decoder_5_out8);
  not not_96 (WO1, decoder_5_out9);
  not not_97 (WO2, decoder_5_out10);
  not not_98 (WO3, decoder_5_out11);
  // NOT_Gate not_99 has open pins: in=decoder_5_out12, out=open
  // NOT_Gate not_100 has open pins: in=decoder_5_out13, out=open
  // NOT_Gate not_101 has open pins: in=decoder_5_out14, out=open
  // NOT_Gate not_102 has open pins: in=decoder_5_out15, out=open
  and and_48 (and_48_out, to_VRAM, Store);
  assign {BYTE_3_2_data, BYTE_2_2_data, BYTE_1_2_data, BYTE_0_2_data} = and_48_out ? GPU_DATA : 32'bz;  // Controlled_Buffer controlled_buffer_24
  assign GPU_DATA = and_49_out ? {BYTE_3_2_data, BYTE_2_2_data, BYTE_1_2_data, BYTE_0_2_data} : 32'bz;  // Controlled_Buffer controlled_buffer_25
  and and_49 (and_49_out, to_VRAM, Load);
  // Probe on out_7
  and and_50 (and_50_out, Clock, ~to_VRAM);  // AND_Gate
  Counter #(.max('h108), .width(9)) counter_2 (
    .Q({counter_2_q[8], GPU_ADR[2:0], counter_2_q[4:0]}), .carry(counter_2_carry), .clk(and_50_out));  // open: load, D, count, clr
  not not_103 (Load_BYPASS, to_VRAM);
  Button button_3 (.out(button_3_out));
  // RGB_Video #(.height(256), .width(256)) rgb_video_1: pin names not known; wires that end beside it: button_3_out, and_50_out, 1'b1, {GPU_ADR[2:0], counter_2_q[4:0]}, GPU_ADR[10:3], rgb_video_1_p6
  Counter #(.max('h96)) counter_3 (.Q(GPU_ADR[10:3]), .clk(counter_2_carry));  // open: load, D, count, carry, clr
  Pull_Resistor pull_resistor_5 (.node({BYTE_3_2_data, BYTE_2_2_data, BYTE_1_2_data, BYTE_0_2_data}));
  Multiplexer #(.enable("false"), .select(4)) multiplexer_2 (
    .in0(BYTE_0_2_data[0]), .in1(BYTE_0_2_data[1]), .in2(BYTE_0_2_data[2]), .in3(BYTE_0_2_data[3]),
    .in4(BYTE_0_2_data[4]), .in5(BYTE_0_2_data[5]), .in6(BYTE_0_2_data[6]), .in7(BYTE_0_2_data[7]),
    .in8(BYTE_1_2_data[0]), .in9(BYTE_1_2_data[1]), .in10(BYTE_1_2_data[2]), .in11(BYTE_1_2_data[3]),
    .in12(BYTE_1_2_data[4]), .in13(BYTE_1_2_data[5]), .in14(BYTE_1_2_data[6]), .in15(BYTE_1_2_data[7]),
    .out(multiplexer_2_out), .sel(counter_2_q[3:0]));
  Multiplexer #(.enable("false"), .select(4)) multiplexer_3 (
    .in0(BYTE_2_2_data[0]), .in1(BYTE_2_2_data[1]), .in2(BYTE_2_2_data[2]), .in3(BYTE_2_2_data[3]),
    .in4(BYTE_2_2_data[4]), .in5(BYTE_2_2_data[5]), .in6(BYTE_2_2_data[6]), .in7(BYTE_2_2_data[7]),
    .in8(BYTE_3_2_data[0]), .in9(BYTE_3_2_data[1]), .in10(BYTE_3_2_data[2]), .in11(BYTE_3_2_data[3]),
    .in12(BYTE_3_2_data[4]), .in13(BYTE_3_2_data[5]), .in14(BYTE_3_2_data[6]), .in15(BYTE_3_2_data[7]),
    .out(multiplexer_3_out), .sel(counter_2_q[3:0]));
  Multiplexer multiplexer_4 (
    .in0(multiplexer_2_out), .in1(multiplexer_3_out), .out(multiplexer_4_out), .sel(counter_2_q[4]), .en(1'b1));
  Multiplexer #(.enable("false"), .width(24)) multiplexer_5 (
    .in0({24{1'b0}}), .in1({24{1'b1}}), .out(rgb_video_1_p6), .sel(multiplexer_4_out));
  // OR_Gate or_3 is placed but not wired

  assign GPU_ADDR = Adress[12:2];

  // Other names for the same wires on the sheet: Adr[31:0] = Adress; Byte_adr[1:0] = Adress[1:0];
  //   Funct_3[2:0] = Funct3; RAM_adress[16:0] = Adress[18:2]; VRAM_adress[10:0] = Adress[12:2];
  //   Store_to_VRAM = Adress[30]; Store_to_Special_registers = Adress[31]; clk = Clock; G4 = B1; G6 = B3; H2 = G7;
  //   S4[7:0] = in1; in1_ac = out_9; S5[7:0] = in2; Input_data[31:0] = Data; Memory_data[31:0] = GPU_DATA;
  //   SR_input[7:0] = GPU_DATA[7:0]; W0 = G3

  // Notes on the sheet:
  //   Register 0
  //   Register 1
  //   Register 2
  //   Register 3
  //   Register 4
  //   Register 5
  //   Register 6
  //   Register 7
  //   Special Registers
  //   In
  //   Special Registers
  //   ** Note: not all registers are in the final version
  //   DATA MEMORY
  //   First Input
  //   Second Input
  //   Unaligned adressing detector
  //   Storing data
  //   SRAM selector - for store
  //   Byte steering logic - input
  //   VRAM selector - for store
  //   SRAM
  //   Function decoder
  //   byte
  //   VRAM_ADRESS
  //   RAM_ADRESS
  //   Loading data
  //   ** Note: this is not the same as on the final version, cause I cannot create a dual-port RAM here
  //   (But it behaves in a similar way)
  //   VRAM
  //   Function decoder for byte steering
  //   Byte
  //   Half
  //   Byte steering logic - output
  //   Function decoder
  //   Imitation of a connected VGA monitor (cropped)
endmodule

module Imm_generator (
  input  [31:0] Ins,
  input  [2:0] Sel,
  output [31:0] Out
);

  wire and_1_out, and_2_out, and_3_out, and_5_out, and_7_out, and_8_out, and_9_out, and_10_out,
       decoder_1_out0, decoder_1_out1, decoder_1_out2, decoder_1_out3, decoder_1_out4, decoder_1_out5,
       decoder_1_out6, decoder_1_out7, decoder_2_out0, decoder_2_out1, decoder_2_out2, decoder_2_out3,
       decoder_2_out4, not_1_out, not_2_out, not_3_out, not_4_out, not_5_out, not_9_out, not_10_out,
       not_11_out, not_12_out, not_13_out, not_14_out, not_15_out, not_16_out, not_17_out, not_18_out,
       not_19_out, not_20_out, not_21_out, not_22_out;
  wire [0:0] and_4_out, and_6_out;
  wire [3:3] or_1_out;

  not not_1 (not_1_out, decoder_1_out0);
  not not_2 (not_2_out, decoder_1_out1);
  not not_3 (not_3_out, decoder_1_out2);
  not not_4 (not_4_out, decoder_1_out3);
  not not_5 (not_5_out, decoder_1_out4);
  // NOT_Gate not_6 has open pins: in=decoder_1_out5, out=open
  // NOT_Gate not_7 has open pins: in=decoder_1_out6, out=open
  // NOT_Gate not_8 has open pins: in=decoder_1_out7, out=open
  Decoder #(.enable("false"), .select(3)) decoder_1 (
    .out0(decoder_1_out0), .out1(decoder_1_out1), .out2(decoder_1_out2), .out3(decoder_1_out3),
    .out4(decoder_1_out4), .out5(decoder_1_out5), .out6(decoder_1_out6), .out7(decoder_1_out7), .sel(Sel));
  LED I_Type (.in(not_1_out));
  LED S_Type (.in(not_2_out));
  LED SB_Type (.in(not_3_out));
  LED U_Type (.in(not_4_out));
  LED UJ_Type (.in(not_5_out));
  and and_1 (and_1_out, not_3_out, and_2_out);
  and and_2 (and_2_out, not_2_out, not_1_out);
  and and_3 (and_3_out, not_3_out, not_2_out);
  not not_9 (not_9_out, not_2_out);
  and and_4 (and_4_out[0], not_9_out, Ins[7]);
  not not_10 (not_10_out, and_3_out);
  or or_1 (or_1_out[3], and_5_out, and_8_out);
  and and_5 (and_5_out, Ins[31], not_11_out);
  not not_11 (not_11_out, and_2_out);
  assign Out[15:8] = not_12_out ? {{4{Ins[31]}}, or_1_out[3], Ins[30:28]} : 8'bz;  // Controlled_Buffer controlled_buffer_1
  not not_12 (not_12_out, and_1_out);
  not not_13 (not_13_out, and_1_out);
  not not_14 (not_14_out, not_1_out);
  and and_6 (and_6_out[0], not_14_out, Ins[20]);
  assign Out[7:0] = not_15_out ? {Ins[27:21], and_6_out[0]} : 8'bz;  // Controlled_Buffer controlled_buffer_2
  not not_15 (not_15_out, and_7_out);
  and and_7 (and_7_out, not_5_out, not_1_out);
  assign {Out[23:20], Out[11:8]} = not_16_out ? {{4{Ins[31]}}, Ins[20], Ins[30:28]} : 8'bz;  // Controlled_Buffer controlled_buffer_3
  not not_16 (not_16_out, not_5_out);
  assign Out[27:20] = not_18_out ? Ins[27:20] : 8'bz;  // Controlled_Buffer controlled_buffer_4
  assign {Out[11:8], Out[31:28]} = not_17_out ? {4'b0000, Ins[31:28]} : 8'bz;  // Controlled_Buffer controlled_buffer_5
  not not_17 (not_17_out, not_4_out);
  not not_18 (not_18_out, not_4_out);
  assign Out[7:0] = not_10_out ? {Ins[27:25], Ins[11:8], and_4_out[0]} : 8'bz;  // Controlled_Buffer controlled_buffer_6
  and and_8 (and_8_out, Ins[7], not_19_out);
  not not_19 (not_19_out, not_3_out);
  assign Out[23:16] = not_13_out ? {8{Ins[31]}} : 8'bz;  // Controlled_Buffer controlled_buffer_7
  assign Out[31:24] = not_20_out ? {8{Ins[31]}} : 8'bz;  // Controlled_Buffer controlled_buffer_8
  not not_20 (not_20_out, and_9_out);
  and and_9 (and_9_out, not_5_out, and_1_out);
  assign Out[7:0] = not_22_out ? {8{1'b0}} : 8'bz;  // Controlled_Buffer controlled_buffer_9
  assign Out[19:12] = not_21_out ? Ins[19:12] : 8'bz;  // Controlled_Buffer controlled_buffer_10
  not not_21 (not_21_out, and_10_out);
  not not_22 (not_22_out, not_4_out);
  and and_10 (and_10_out, not_4_out, not_5_out);
  Pull_Resistor pull_resistor_1 (.node(Out));
  Decoder #(.enable("false"), .select(3)) decoder_2 (
    .out0(decoder_2_out0), .out1(decoder_2_out1), .out2(decoder_2_out2), .out3(decoder_2_out3),
    .out4(decoder_2_out4), .sel(Sel));  // open: out5, out6, out7
  LED I_Type_2 (.in(decoder_2_out0));
  LED S_Type_2 (.in(decoder_2_out1));
  LED SB_Type_2 (.in(decoder_2_out2));
  LED U_Type_2 (.in(decoder_2_out3));
  LED UJ_Type_2 (.in(decoder_2_out4));

  // Other names for the same wires on the sheet: Select[2:0] = Sel

  // Notes on the sheet:
  //   "Optimized" immediate generator
  //   Just for output LEDs (not in actual CPU)
endmodule

module shifter (
  input  in_1,
  input  [2:0] in_2,
  input  [31:0] in_3,
  input  [4:0] in_4,
  output [31:0] out_5,
  output SH_out
);

  wire and_1_out, not_1_out, not_2_out, not_3_out, not_4_out, not_5_out, shift_to_left, shift_to_right;
  wire [0:0] controlled_buffer_1_out;
  wire [31:0] controlled_buffer_1_out_2, controlled_buffer_3_out, controlled_buffer_5_out,
       controlled_buffer_7_out, controlled_buffer_9_out, controlled_buffer_11_out;
  wire [31:31] and_3_out, and_4_out, and_5_out, and_6_out;

  // Probe on in_3
  assign {controlled_buffer_1_out_2[30:0], controlled_buffer_1_out[0]} = shift_to_left ? {in_3[0], in_3[1], in_3[2], in_3[3], in_3[4], in_3[5], in_3[6], in_3[7], in_3[8], in_3[9], in_3[10], in_3[11], in_3[12], in_3[13], in_3[14], in_3[15], in_3[16], in_3[17], in_3[18], in_3[19], in_3[20], in_3[21], in_3[22], in_3[23], in_3[24], in_3[25], in_3[26], in_3[27], in_3[28], in_3[29], in_3[30], in_3[31]} : 32'bz;  // Controlled_Buffer controlled_buffer_1
  assign {controlled_buffer_1_out_2[30:0], controlled_buffer_1_out[0]} = shift_to_right ? in_3 : 32'bz;  // Controlled_Buffer controlled_buffer_2
  // Probe on {controlled_buffer_1_out_2[30:0], controlled_buffer_1_out[0]}
  and and_1 (and_1_out, shift_to_right, in_1);
  not not_1 (not_1_out, in_4[0]);
  and and_2 (controlled_buffer_1_out_2[31], controlled_buffer_1_out_2[30], and_1_out);
  // Probe on controlled_buffer_3_out
  assign controlled_buffer_3_out = not_1_out ? {controlled_buffer_1_out_2[30:0], controlled_buffer_1_out[0]} : 32'bz;  // Controlled_Buffer controlled_buffer_3
  assign controlled_buffer_3_out = in_4[0] ? controlled_buffer_1_out_2 : 32'bz;  // Controlled_Buffer controlled_buffer_4
  Decoder #(.enable("false"), .select(3)) decoder_1 (
    .out1(shift_to_left), .out5(shift_to_right), .sel(in_2));  // open: out0, out2, out3, out4, out6, out7
  assign controlled_buffer_5_out = not_2_out ? controlled_buffer_3_out : 32'bz;  // Controlled_Buffer controlled_buffer_5
  not not_2 (not_2_out, in_4[1]);
  assign controlled_buffer_5_out = in_4[1] ? {{2{and_3_out[31]}}, controlled_buffer_3_out[31:2]} : 32'bz;  // Controlled_Buffer controlled_buffer_6
  and and_3 (and_3_out[31], controlled_buffer_3_out[31], and_1_out);
  // Probe on controlled_buffer_5_out
  // Probe on controlled_buffer_7_out
  assign controlled_buffer_7_out = not_3_out ? controlled_buffer_5_out : 32'bz;  // Controlled_Buffer controlled_buffer_7
  not not_3 (not_3_out, in_4[2]);
  assign controlled_buffer_7_out = in_4[2] ? {{4{and_4_out[31]}}, controlled_buffer_5_out[31:4]} : 32'bz;  // Controlled_Buffer controlled_buffer_8
  and and_4 (and_4_out[31], controlled_buffer_5_out[31], and_1_out);
  and and_5 (and_5_out[31], controlled_buffer_7_out[31], and_1_out);
  // Probe on controlled_buffer_9_out
  assign controlled_buffer_9_out = not_4_out ? controlled_buffer_7_out : 32'bz;  // Controlled_Buffer controlled_buffer_9
  not not_4 (not_4_out, in_4[3]);
  assign controlled_buffer_9_out = in_4[3] ? {{8{and_5_out[31]}}, controlled_buffer_7_out[31:8]} : 32'bz;  // Controlled_Buffer controlled_buffer_10
  or or_1 (SH_out, shift_to_left, shift_to_right);
  and and_6 (and_6_out[31], controlled_buffer_9_out[31], and_1_out);
  // Probe on controlled_buffer_11_out
  assign controlled_buffer_11_out = not_5_out ? controlled_buffer_9_out : 32'bz;  // Controlled_Buffer controlled_buffer_11
  not not_5 (not_5_out, in_4[4]);
  assign controlled_buffer_11_out = in_4[4] ? {{16{and_6_out[31]}}, controlled_buffer_9_out[31:16]} : 32'bz;  // Controlled_Buffer controlled_buffer_12
  // Probe on out_5
  assign out_5 = shift_to_left ? {controlled_buffer_11_out[0], controlled_buffer_11_out[1], controlled_buffer_11_out[2], controlled_buffer_11_out[3], controlled_buffer_11_out[4], controlled_buffer_11_out[5], controlled_buffer_11_out[6], controlled_buffer_11_out[7], controlled_buffer_11_out[8], controlled_buffer_11_out[9], controlled_buffer_11_out[10], controlled_buffer_11_out[11], controlled_buffer_11_out[12], controlled_buffer_11_out[13], controlled_buffer_11_out[14], controlled_buffer_11_out[15], controlled_buffer_11_out[16], controlled_buffer_11_out[17], controlled_buffer_11_out[18], controlled_buffer_11_out[19], controlled_buffer_11_out[20], controlled_buffer_11_out[21], controlled_buffer_11_out[22], controlled_buffer_11_out[23], controlled_buffer_11_out[24], controlled_buffer_11_out[25], controlled_buffer_11_out[26], controlled_buffer_11_out[27], controlled_buffer_11_out[28], controlled_buffer_11_out[29], controlled_buffer_11_out[30], controlled_buffer_11_out[31]} : 32'bz;  // Controlled_Buffer controlled_buffer_13
  assign out_5 = shift_to_right ? controlled_buffer_11_out : 32'bz;  // Controlled_Buffer controlled_buffer_14

  // Other names for the same wires on the sheet: input_data[31:0] = in_3; funct3[2:0] = in_2; is_arithmetic = in_1;
  //   shift_by[4:0] = in_4; shifted_data[31:0] = out_5

  // Notes on the sheet:
  //   Input reverse
  //   (if shifting to left)
  //   Not sure if this gate is needed as the "i" should never be "1" in left shift
  //   Inputs
  //   i: 31st bit of ins
  //   input data (from RB0)
  //   shift by (from RB1)
  //   | ins | func3 | i |
  //   | SLL | 001 | x |
  //   | SRL | 101 | 0 |
  //   | SRA | 101 | 1 |
  //   funct3
  //   Outputs
  //   Output reverse
  //   (if shifting to left)
endmodule
